# Fritzing sketch 7Segment_direct (saved by Fritzing 0.8.5b)
circuit board: 6.88566cm x 5.36311cm
breadboards: 2

parts:
  Digit_4 = 7 Segment Display
  Digit_3 = 7 Segment Display
  Digit_2 = 7 Segment Display
  Digit_1 = 7 Segment Display
  Arduino1 = Arduino Uno (Rev3)

nets:
  N1: Digit_4.Segment_E, Digit_3.Segment_E, Digit_2.Segment_E, Digit_1.Segment_E, Arduino1.D6_PWM
  N2: Digit_4.Segment_D, Digit_3.Segment_D, Digit_2.Segment_D, Digit_1.Segment_D, Arduino1.D5_PWM
  N3: Digit_4.common_anode, Arduino1.D13/SCK
  N4: Digit_4.Segment_C, Digit_3.Segment_C, Digit_2.Segment_C, Digit_1.Segment_C
  N5: Digit_4.Segment_DP, Digit_3.Segment_DP, Digit_2.Segment_DP, Digit_1.Segment_DP, Arduino1.D4
  N6: Digit_4.Segment_B, Digit_3.Segment_B, Digit_2.Segment_B, Digit_1.Segment_B, Arduino1.D3_PWM
  N7: Digit_4.Segment_A, Digit_3.Segment_A, Digit_2.Segment_A, Digit_1.Segment_A, Arduino1.D2
  N8: Digit_4.Segment_F, Digit_3.Segment_F, Digit_2.Segment_F, Digit_1.Segment_F, Arduino1.D7
  N9: Digit_4.Segment_G, Digit_3.Segment_G, Digit_2.Segment_G, Digit_1.Segment_G, Arduino1.D8
  N10: Digit_3.common_anode, Arduino1.D12/MISO
  N11: Digit_2.common_anode, Arduino1.D11_PWM/MOSI
  N12: Digit_1.common_anode, Arduino1.D10_PWM/SS
