# Fritzing sketch AnalogInputFSR (saved by Fritzing 0.8.0b)
breadboards: 2

parts:
  J1 = Basic Force Sensing Resistor (FSR) [package=THT]
  R2 = Resistor [resistance=10k tolerance=±5% package=THT]
  LED2 = LED - 5mm [color="Red (633nm)" package="5 mm [THT]"]
  Arduino2 = Arduino Uno (Rev3)

nets:
  N1: J1.pin_0, Arduino2.5V
  N2: J1.pin_1, R2.Pin_1, Arduino2.A2
  N3: R2.Pin_0, LED2.cathode, Arduino2.GND
  N4: LED2.anode, Arduino2.D13/SCK

notes:
  In this example, FSR values are read in through an 'Analog In' pin. The values are then used to control the blinking rate of an LED.
  Related examples: http://www.ladyada.net/learn/sensors/fsr.html
  http://itp.nyu.edu/physcomp/sensors/Reports/ForceSensorResistor
  Related code: http://arduino.cc/en/Tutorial/AnalogInput

// code stored in the sketch: AnalogInputFSR.ino
/*
  Analog Input
 Demonstrates analog input by reading an analog sensor on analog pin 0 and
 turning on and off a light emitting diode(LED)  connected to digital pin 13. 
 The amount of time the LED will be on and off depends on
 the value obtained by analogRead(). 
 
 The circuit:
 * Potentiometer attached to analog input 0
 * center pin of the potentiometer to the analog pin
 * one side pin (either one) to ground
 * the other side pin to +5V
 * LED anode (long leg) attached to digital output 13
 * LED cathode (short leg) attached to ground
 
 * Note: because most Arduinos have a built-in LED attached 
 to pin 13 on the board, the LED is optional.
 
 
 Created by David Cuartielles
 modified 30 Aug 2011
 By Tom Igoe
 
 This example code is in the public domain.
 
 http://arduino.cc/en/Tutorial/AnalogInput
 
 */

int sensorPin = 2;    // select the input pin for the potentiometer
int ledPin = 13;      // select the pin for the LED
int sensorValue = 0;  // variable to store the value coming from the sensor

void setup() {
  // declare the ledPin as an OUTPUT:
  pinMode(ledPin, OUTPUT);  
}

void loop() {
  // read the value from the sensor:
  sensorValue = analogRead(sensorPin);    
  // turn the ledPin on
  digitalWrite(ledPin, HIGH);  
  // stop the program for <sensorValue> milliseconds:
  delay(sensorValue);          
  // turn the ledPin off:        
  digitalWrite(ledPin, LOW);   
  // stop the program for for <sensorValue> milliseconds:
  delay(sensorValue);                  
}

// code stored in the sketch: Untitled.ino
/*
  Analog Input
 Demonstrates analog input by reading an analog sensor on analog pin 0 and
 turning on and off a light emitting diode(LED)  connected to digital pin 13. 
 The amount of time the LED will be on and off depends on
 the value obtained by analogRead(). 
 
 The circuit:
 * Potentiometer attached to analog input 0
 * center pin of the potentiometer to the analog pin
 * one side pin (either one) to ground
 * the other side pin to +5V
 * LED anode (long leg) attached to digital output 13
 * LED cathode (short leg) attached to ground
 
 * Note: because most Arduinos have a built-in LED attached 
 to pin 13 on the board, the LED is optional.
 
 
 Created by David Cuartielles
 modified 30 Aug 2011
 By Tom Igoe
 
 This example code is in the public domain.
 
 http://arduino.cc/en/Tutorial/AnalogInput
 
 */

int sensorPin = 2;    // select the input pin for the potentiometer
int ledPin = 13;      // select the pin for the LED
int sensorValue = 0;  // variable to store the value coming from the sensor

void setup() {
  // declare the ledPin as an OUTPUT:
  pinMode(ledPin, OUTPUT);  
}

void loop() {
  // read the value from the sensor:
  sensorValue = analogRead(sensorPin);    
  // turn the ledPin on
  digitalWrite(ledPin, HIGH);  
  // stop the program for <sensorValue> milliseconds:
  delay(sensorValue);          
  // turn the ledPin off:        
  digitalWrite(ledPin, LOW);   
  // stop the program for for <sensorValue> milliseconds:
  delay(sensorValue);                  
}
