# Fritzing sketch EDGY-motor-control (saved by Fritzing 0.8.0b)
breadboards: 2

parts:
  EDGY_motor_control1 = EDGY
  M1 = DC Motor
  Arduino1 = Arduino Uno (Rev3)

nets:
  N1: EDGY_motor_control1.A1, Arduino1.D5_PWM
  N2: EDGY_motor_control1.B1, Arduino1.D4
  N3: EDGY_motor_control1.Speed1, Arduino1.D3_PWM
  VIN: EDGY_motor_control1.Vin, EDGY_motor_control1.5V+, Arduino1.5V
  GND: EDGY_motor_control1.GND, Arduino1.GND
  N4: EDGY_motor_control1.B1out, M1.pin_2
  N5: EDGY_motor_control1.A1out, M1.pin_1

// code stored in the sketch: EDGY-motor-control.ino
int m1Pin = 5;
int m2Pin = 4;
int speed1Pin = 3;

void setup() {
  pinMode(m1Pin,OUTPUT);
  pinMode(m2Pin,OUTPUT);
}

void loop() {
for(int fadeValue = 0 ; fadeValue <= 255; fadeValue +=5) {
analogWrite(speed1Pin, fadeValue);
digitalWrite(m1Pin,HIGH);
digitalWrite(m2Pin,LOW);
delay(30);
}
delay(1000);
for(int fadeValue = 255 ; fadeValue >= 0; fadeValue -=5) {
analogWrite(speed1Pin, fadeValue);
digitalWrite(m2Pin,HIGH);
digitalWrite(m1Pin,LOW);
delay(30);
}
delay(1000);
}
