# Fritzing sketch H-Bridge (saved by Fritzing 0.8.6b)
circuit board: 6.88566cm x 5.36311cm
breadboards: 2

parts:
  L293D = L293D [package=THT]
  Motor2 = DC Motor
  VCC = Battery block 9V
  Motor1 = DC Motor
  Bauteil1 = Arduino Uno (Rev3)
  part = Battery block 9V  # not connected

nets:
  N1: L293D.Enable_1, Bauteil1.D3_PWM
  N2: L293D.In_1, Bauteil1.D6_PWM
  N3: L293D.Out_1_(_Controlled_by_Enable_1_), Motor2.pin_2
  N4: L293D.0V, VCC.-, Bauteil1.GND
  N5: L293D.Out_2_(_Controlled_by_Enable_1_), Motor2.pin_1
  N6: L293D.In_2, Bauteil1.D5_PWM
  N7: L293D.+Vmotor, VCC.+, Bauteil1.VIN
  N8: L293D.Enable_2, Bauteil1.D9_PWM
  N9: L293D.In_3, Bauteil1.D11_PWM/MOSI
  N10: L293D.Out_3_(_Controlled_by_Enable_2_), Motor1.pin_2
  N11: L293D.Out_4_(_Controlled_by_Enable_2_), Motor1.pin_1
  N12: L293D.In_4, Bauteil1.D10_PWM/SS
  N13: L293D.+V, Bauteil1.5V

notes:
  H-BRIDGE
