# Fritzing sketch Verstaerkung (saved by Fritzing 0.8.6b)
circuit board: 6.88566cm x 5.36311cm
breadboards: 2

parts:
  Motor = DC Motor
  Batterie = Battery block 9V
  FET = Basic FET N-Channel [package="TO220 [THT]"]
  Arduino1 = Arduino Uno (Rev3)
  part = Basic FET N-Channel [package="TO220 [THT]"]  # not connected

nets:
  N1: Motor.pin_1, FET.drain
  N2: Motor.pin_2, Batterie.+
  N3: Batterie.-, FET.source, Arduino1.GND
  N4: FET.gate, Arduino1.D9_PWM

notes:
  +
  -
  VERSTAERKUNG
