# Fritzing sketch Automatic_Lighting_System (saved by Fritzing 0.8.4b)
circuit board: 6.88566cm x 5.36311cm
breadboards: 2

parts:
  LED1 = LED - 5mm [color="White (6500K)" package="5 mm [THT]"]
  R1 = Resistor [tolerance=±5% resistance=220 package=THT]
  R2 = Resistor [tolerance=±5% resistance=220 package=THT]
  LED2 = LED - 5mm [color="White (6500K)" package="5 mm [THT]"]
  Light_Resistance = Photocell (LDR) [package=THT]
  R3 = Resistor [tolerance=±5% resistance=100k package=THT]
  Bauteil1 = Arduino Uno (Rev3)

nets:
  N1: LED1.cathode, R1.Pin_0
  N2: LED1.anode, LED2.anode, Bauteil1.D2
  N3: R1.Pin_1, R2.Pin_1, Light_Resistance.pin_0, Bauteil1.GND
  N4: R2.Pin_0, LED2.cathode
  N5: Light_Resistance.pin_1, R3.Pin_0, Bauteil1.A0
  N6: R3.Pin_1, Bauteil1.5V

notes:
  LIGHTING SYSTEM
