# Fritzing sketch MidiDrumKit (saved by Fritzing 0.8.6b)
circuit board: 6.88566cm x 5.36311cm
breadboards: 2

parts:
  R1 = Resistor [resistance=1M tolerance=±5% package=THT]
  R1_2 = Resistor [resistance=1M tolerance=±5% package=THT]
  S1 = Pushbutton [package="[THT]"]
  S2 = Pushbutton [package="[THT]"]
  S3 = Pushbutton [package="[THT]"]
  R1_3 = Resistor [resistance=100k tolerance=±5% package=THT]
  R1_4 = Resistor [resistance=100k tolerance=±5% package=THT]
  R1_5 = Resistor [resistance=100k tolerance=±5% package=THT]
  DIN1 = DIN-5 jack (MIDI) [package=THT]
  R2 = Resistor [resistance=220 tolerance=±5% package=THT]
  Zener1 = Zener Diode [part_number=1N4732A breakdown_voltage=3.6V package="300 mil [THT]"]
  Zener2 = Zener Diode [part_number=1N4732A breakdown_voltage=3.6V package="300 mil [THT]"]
  J1 = Piezo Speaker
  J1_2 = Piezo Speaker
  MIDI_Drum_Kit = Arduino Uno (Rev3)
  part = Piezo Speaker  # not connected

nets:
  N1: R1.Pin_0, Zener1.cathode, J1_2.pin2, MIDI_Drum_Kit.A1
  N2: R1.Pin_1, R1_2.Pin_1, S1.Pin_3, S1.Pin_4, S2.Pin_3, S2.Pin_4, S3.Pin_3, S3.Pin_4, R1_3.Pin_1, R1_4.Pin_1, R1_5.Pin_1, DIN1.2, Zener1.anode, Zener2.anode, J1.pin1, J1_2.pin1, MIDI_Drum_Kit.GND
  N3: R1_2.Pin_0, Zener2.cathode, J1.pin2, MIDI_Drum_Kit.A0
  N4: S1.Pin_1, S1.Pin_2, R1_3.Pin_0, MIDI_Drum_Kit.D7
  N5: S2.Pin_1, S2.Pin_2, R1_4.Pin_0, MIDI_Drum_Kit.D6_PWM
  N6: S3.Pin_1, S3.Pin_2, R1_5.Pin_0, MIDI_Drum_Kit.D5_PWM
  N7: DIN1.5, MIDI_Drum_Kit.D1/TX
  N8: DIN1.4, R2.Pin_0
  N9: R2.Pin_1, MIDI_Drum_Kit.5V

notes:
  Arduino MIDI Drum Shield
  from todbot.com
  Diodes should be 5.1 V Zener diodes
