# Fritzing sketch Op-amp (saved by Fritzing 0.8.6b)
circuit board: 6.88566cm x 5.36311cm
breadboards: 2

parts:
  J1 = Basic Force Sensing Resistor (FSR) [package=THT]
  R3 = Resistor [resistance=6.8k tolerance=±5% package=THT]
  R4 = Resistor [tolerance=±5% resistance=220 package=THT]
  LED1 = LED - 5mm [color="Red (633nm)" package="5 mm [THT]"]
  U1 = LM 358 Dual Op-Amp [package="DIP8 [THT]"]
  Arduino1 = Arduino Uno (Rev3)

nets:
  N1: J1.pin_0, U1.connector7, Arduino1.5V
  N2: J1.pin_1, R3.Pin_0, U1.connector2
  N3: R3.Pin_1, LED1.cathode, U1.connector3, Arduino1.GND
  N4: R4.Pin_0, LED1.anode
  N5: R4.Pin_1, Arduino1.D9_PWM
  N6: U1.connector0, U1.connector1, Arduino1.A2

notes:
  In this example, an LM 358 Dual Operational Amplifier is used to get a stronger, more stable signal from an FSR. You can use this configuration with any resistive sensor. Feel free to place a small ceramic cap between PIN1 on the Opamp and GND to make the signal smoother.
  http://itp.nyu.edu/physcomp/sensors/Schematics/LM358OpAmp

// code stored in the sketch: Op-amp.ino
int ledPin=9;	// where the LED is connected to
int fsrPin = 2;  // where the FSR is connected to

int value; 

void setup(){

}

void loop(){
	value = analogRead(fsrPin);
	analogWrite(ledPin,value/4);		
	delay(10);						// just for breathing
}
