# Fritzing sketch Relay (saved by Fritzing 0.8.6b)
circuit board: 6.88566cm x 5.36311cm
breadboards: 2

parts:
  Power_plug2 = Power plug
  M2 = DC Motor
  D3 = Rectifier Diode [part_number=1N4001 package="300 mil [THT]"]
  R4 = Resistor [resistance=1k tolerance=±5% package=THT]
  K2 = Relay [part_number=FRS1B-S package=THT]
  Q3 = NPN-Transistor [package="TO92 [THT]"]
  Arduino1 = Arduino Uno (Rev3)
  part = NPN-Transistor [package="TO92 [THT]"]  # not connected

nets:
  N1: Power_plug2.GND, M2.pin_2
  N2: Power_plug2.VCC, K2.C1, K2.C2
  N3: M2.pin_1, K2.A
  N4: D3.cathode, K2.COIL2, Arduino1.5V
  N5: D3.anode, K2.COIL1, Q3.C
  N6: R4.Pin_0, Q3.B
  N7: R4.Pin_1, Arduino1.D3_PWM
  N8: Q3.E, Arduino1.GND

notes:
  In this circuit a 5V relay is connected to the arduino board and controls a DC motor which is connected to an external power supply.
