# Fritzing sketch Shift_Register (saved by Fritzing 0.8.0b)
breadboards: 2

parts:
  Arduino1 = Arduino Uno (Rev3)
  R10 = Resistor [resistance=220 tolerance=±5% package=THT]
  R11 = Resistor [resistance=220 tolerance=±5% package=THT]
  R12 = Resistor [resistance=220 tolerance=±5% package=THT]
  R13 = Resistor [resistance=220 tolerance=±5% package=THT]
  R14 = Resistor [resistance=220 tolerance=±5% package=THT]
  R15 = Resistor [resistance=220 tolerance=±5% package=THT]
  R16 = Resistor [resistance=220 tolerance=±5% package=THT]
  R17 = Resistor [resistance=220 tolerance=±5% package=THT]
  LED10 = LED - 5mm [color="Red (633nm)" package="5 mm [THT]"]
  LED11 = LED - 5mm [color="Red (633nm)" package="5 mm [THT]"]
  LED12 = LED - 5mm [color="Red (633nm)" package="5 mm [THT]"]
  LED13 = LED - 5mm [color="Red (633nm)" package="5 mm [THT]"]
  LED14 = LED - 5mm [color="Red (633nm)" package="5 mm [THT]"]
  LED15 = LED - 5mm [color="Red (633nm)" package="5 mm [THT]"]
  LED16 = LED - 5mm [color="Red (633nm)" package="5 mm [THT]"]
  LED17 = LED - 5mm [color="Red (633nm)" package="5 mm [THT]"]
  74HC5952 = 74HC595 [package="DIP16 [THT]"]
  C3 = Ceramic Capacitor [capacitance=100nF rated_voltage=35V package="200 mil [THT, multilayer]"]

nets:
  N1: Arduino1.ICSP_MISO, Arduino1.D12/MISO, 74HC5952.SH_CP
  N2: Arduino1.ICSP_MOSI, Arduino1.D11_PWM/MOSI, 74HC5952.DS
  GND: Arduino1.GND, LED10.cathode, LED11.cathode, LED12.cathode, LED13.cathode, LED14.cathode, LED15.cathode, LED16.cathode, LED17.cathode, 74HC5952.GND, 74HC5952.OE, C3.1
  N3: Arduino1.D8, 74HC5952.ST_CP, C3.0
  5V: Arduino1.5V, 74HC5952.MR, 74HC5952.VCC
  N4: R10.Pin_0, LED14.anode
  N5: R10.Pin_1, 74HC5952.Q6
  N6: R11.Pin_0, LED10.anode
  N7: R11.Pin_1, 74HC5952.Q5
  N8: R12.Pin_0, LED12.anode
  N9: R12.Pin_1, 74HC5952.Q4
  N10: R13.Pin_0, LED11.anode
  N11: R13.Pin_1, 74HC5952.Q7
  N12: R14.Pin_0, LED13.anode
  N13: R14.Pin_1, 74HC5952.Q3
  N14: R15.Pin_0, LED15.anode
  N15: R15.Pin_1, 74HC5952.Q2
  N16: R16.Pin_0, LED16.anode
  N17: R16.Pin_1, 74HC5952.Q1
  N18: R17.Pin_0, LED17.anode
  N19: R17.Pin_1, 74HC5952.Q0

notes:
  In this project, a 74HC595 shift register is used to control 8 LEDs with just 3 Arduino pins.
  Related example: http://www.arduino.cc/en/Tutorial/ShiftOut

// code stored in the sketch: Shift_Register.ino
/*
  Shift Register Example
 for 74HC595 shift register

 This sketch turns reads serial input and uses it to set the pins
 of a 74HC595 shift register.

 Hardware:
 * 74HC595 shift register attached to pins 2, 3, and 4 of the Arduino,
 as detailed below.
 * LEDs attached to each of the outputs of the shift register

 Created 22 May 2009
 Created 23 Mar 2010
 by Tom Igoe

 */

//Pin connected to latch pin (ST_CP) of 74HC595
const int latchPin = 8;
//Pin connected to clock pin (SH_CP) of 74HC595
const int clockPin = 12;
////Pin connected to Data in (DS) of 74HC595
const int dataPin = 11;

void setup() {
  //set pins to output because they are addressed in the main loop
  pinMode(latchPin, OUTPUT);
  pinMode(dataPin, OUTPUT);  
  pinMode(clockPin, OUTPUT);
  Serial.begin(9600);
  Serial.println("reset");
}

void loop() {
  if (Serial.available() > 0) {
    // ASCII '0' through '9' characters are
    // represented by the values 48 through 57.
    // so if the user types a number from 0 through 9 in ASCII, 
    // you can subtract 48 to get the actual value:
    int bitToSet = Serial.read() - 48;

  // write to the shift register with the correct bit set high:
    registerWrite(bitToSet, HIGH);
  }
}

// This method sends bits to the shift register:

void registerWrite(int whichPin, int whichState) {
// the bits you want to send
  byte bitsToSend = 0;

  // turn off the output so the pins don't light up
  // while you're shifting bits:
  digitalWrite(latchPin, LOW);

  // turn on the next highest bit in bitsToSend:
  bitWrite(bitsToSend, whichPin, whichState);

  // shift the bits out:
  shiftOut(dataPin, clockPin, MSBFIRST, bitsToSend);

    // turn on the output so the LEDs can light up:
  digitalWrite(latchPin, HIGH);

}
