# Fritzing sketch Stepper_Motor (saved by Fritzing 0.8.5b)
circuit board: 6.88566cm x 5.36311cm
breadboards: 2

parts:
  Arduino1 = Arduino Uno (Rev3)
  M2 = Stepper Motor - Bipolar
  Power_plug2 = Power plug
  R14 = Resistor [resistance=1k tolerance=±5% package=THT]
  R15 = Resistor [resistance=1k tolerance=±5% package=THT]
  R16 = Resistor [resistance=10k tolerance=±5% package=THT]
  R17 = Resistor [resistance=10k tolerance=±5% package=THT]
  IC2 = H-Bridge [package=THT]
  Q8 = NPN-Transistor [package="TO92 [THT]"]
  Q9 = NPN-Transistor [package="TO92 [THT]"]

nets:
  GND: Arduino1.GND, Power_plug2.GND, IC2.GND1, IC2.GND2, IC2.GND3, IC2.GND4, Q8.E, Q9.E
  N1: Arduino1.D10_PWM/SS, R14.Pin_0, IC2.1A
  N2: Arduino1.D11_PWM/MOSI, R15.Pin_1, IC2.4A
  N3: Arduino1.5V, R16.Pin_1, R17.Pin_0, IC2.1_2EN, IC2.3_4EN, IC2.VCC1
  N4: M2.A, IC2.1Y
  N5: M2.C, IC2.2Y
  N6: M2.B, IC2.4Y
  N7: M2.D, IC2.3Y
  N8: Power_plug2.VCC, IC2.VCC2
  N9: R14.Pin_1, Q9.B
  N10: R15.Pin_0, Q8.B
  N11: R16.Pin_0, IC2.3A, Q8.C
  N12: R17.Pin_1, IC2.2A, Q9.C

notes:
  This project shows how to control a stepper motor's direction (running forwards and backwards) using an H-bridge. An H-bridge is an electronic circuit which enables a voltage to be applied across a load in either direction.
  Related Examples:
  Stepper Motor Control
