# Fritzing sketch TouchSwitch (saved by Fritzing 0.8.6b)
circuit board: 6.88566cm x 5.36311cm
breadboards: 2

parts:
  R11 = Resistor [resistance=10k tolerance=±5% package=THT]
  R12 = Resistor [resistance=1k tolerance=±5% package=THT]
  R13 = Resistor [resistance=10k tolerance=±5% package=THT]
  J1 = female pin header, 1 pin [form="♀ (female)"]
  J2 = female pin header, 1 pin [form="♀ (female)"]
  Q7 = NPN-Transistor [package="TO92 [THT]"]
  Q6 = NPN-Transistor [package="TO92 [THT]"]
  Arduino1 = Arduino Uno (Rev3)
  part = Arduino Uno (Rev3)  # not connected

nets:
  N1: R11.Pin_0, Q6.C
  N2: R11.Pin_1, Q7.B
  N3: R12.Pin_0, Q6.E
  N4: R12.Pin_1, R13.Pin_1, J2.pin1, Arduino1.5V
  N5: R13.Pin_0, Q7.E, Arduino1.A0
  N6: J1.pin1, Q6.B
  N7: Q7.C, Arduino1.GND

notes:
  A simple touch switch can be created by using two NPN transistors. When touching the blue and the red cable, the LED will turn on. (download code from the project page)
  http://en.wikipedia.org/wiki/Darlington_transistor
