# Fritzing sketch VirtualColorMixer (saved by Fritzing 0.8.6b)
circuit board: 6.88566cm x 5.36311cm
breadboards: 2

parts:
  R1 = Rotary Potentiometer (Small) [maximum_resistance=100kΩ package=THT]
  R2 = Rotary Potentiometer (Small) [maximum_resistance=100kΩ package=THT]
  R3 = Rotary Potentiometer (Small) [maximum_resistance=100kΩ package=THT]
  Arduino1 = Arduino Uno (Rev3)
  part = Rotary Potentiometer (Small) [maximum_resistance=100kΩ package=THT]  # not connected

nets:
  N1: R1.leg1, R2.leg1, R3.leg1, Arduino1.GND
  N2: R1.wiper, Arduino1.A0
  N3: R1.leg2, R2.leg2, R3.leg2, Arduino1.5V
  N4: R2.wiper, Arduino1.A1
  N5: R3.wiper, Arduino1.A2

notes:
  You can send multiple values from the Arduino board to the computer using the serial print function. In this project, the analog values from three potentiometers are used to set the red, green, and blue values of the background color of a Processing sketch running on the computer.
  http://arduino.cc/en/Tutorial/VirtualColorMixer
