# Fritzing sketch 555TouchSwitch (saved by Fritzing 0.8.6b)
circuit board: 6.88566cm x 5.36311cm
breadboards: 2

parts:
  C3 = Ceramic Capacitor [capacitance=100nF rated_voltage=35V package="200 mil [THT, multilayer]"]
  C4 = Ceramic Capacitor [capacitance=100nF rated_voltage=35V package="200 mil [THT, multilayer]"]
  R2 = Resistor [resistance=100k tolerance=±5% package=THT]
  U2 = 555 Timer [package="DIP8 [THT]"]
  TouchSwitch1 = Antenna
  Arduino1 = Arduino Uno (Rev3)
  part = Resistor [tolerance=±5% resistance=220 package=THT]  # not connected

nets:
  N1: C3.0, C4.1, U2.Ground, Arduino1.GND
  N2: C3.1, R2.Pin_0, U2.Threshold, U2.Discharge
  N3: C4.0, U2.Control_Voltage
  N4: R2.Pin_1, U2.Reset, U2.Vcc_Supply_Voltage, Arduino1.5V
  N5: U2.Trigger, TouchSwitch1.antenna_lead
  N6: U2.Output, Arduino1.D6_PWM

notes:
  This is a 555 timer touch switch circuit based on a Forrest Mims circuit. The yellow wire serves as the touch sensor. Pin 3 on the 555 timer is the output signal and is read by Pin 6 on the Arduino.
  http://talkingelectronics.com/projects/TouchSwitch/TouchSwitch-1.html
