# Fritzing sketch AnalogInputPot (saved by Fritzing 0.8.6b)
circuit board: 6.88566cm x 5.36311cm
breadboards: 2

parts:
  LED2 = LED - 5mm [color="Red (633nm)" package="5 mm [THT]"]
  R1 = Rotary Potentiometer (Small) [maximum_resistance=100kΩ package=THT]
  Arduino2 = Arduino Uno (Rev3)
  part = LED - 5mm [color="Red (633nm)" package="5 mm [THT]"]  # not connected

nets:
  N1: LED2.cathode, R1.leg1, Arduino2.GND
  N2: LED2.anode, Arduino2.D13/SCK
  N3: R1.wiper, Arduino2.A3
  N4: R1.leg2, Arduino2.5V

notes:
  In this example, potentiometer values are read in through an 'Analog In' pin. The values are then used to control the blinking rate of an LED. Related example: http://arduino.cc/en/Tutorial/AnalogInput
