# Fritzing sketch Blink (saved by Fritzing 0.8.0b)
breadboards: 1

parts:
  LED2 = LED - 5mm [color="Red (633nm)" package="5 mm [THT]"]
  R1 = Resistor [tolerance=±5% resistance=220 package=THT]
  Arduino1 = Arduino Uno (Rev3)
  Arduino2 = Arduino Uno (Rev3)
  LED1 = LED - 5mm [color="Red (633nm)" package="5 mm [THT]"]

nets:
  N1: LED2.cathode, R1.Pin_0
  N2: LED2.anode, Arduino1.D13/SCK
  N3: R1.Pin_1, Arduino1.GND
  N4: Arduino2.D13/SCK, LED1.anode
  N5: Arduino2.GND, LED1.cathode

notes:
  While the version above will work, it might damage the LED after some time. Better limit the current that runs through it by adding a resistor.
  The right resistor value can be
  calculated like this.
  In this very simple example, Arduino will be programmed to blink the LED on pin 13.
  Related Arduino example:
  http://arduino.cc/en/Tutorial/Blink

// code stored in the sketch: Blink.ino
/*
  Blink
  Turns on an LED on for one second, then off for one second, repeatedly.
 
  This example code is in the public domain.
 */

void setup() {                
  // initialize the digital pin as an output.
  // Pin 13 has an LED connected on most Arduino boards:
  pinMode(13, OUTPUT);     
}

void loop() {
  digitalWrite(13, HIGH);   // set the LED on
  delay(1000);              // wait for a second
  digitalWrite(13, LOW);    // set the LED off
  delay(1000);              // wait for a second
}
