# Fritzing sketch Button (saved by Fritzing 0.8.5b)
circuit board: 6.88566cm x 5.36311cm
breadboards: 1

parts:
  LED1 = LED - 5mm [color="Red (633nm)" package="5 mm [THT]"]
  Arduino1 = Arduino Uno (Rev3)
  S1 = Pushbutton [package=THT]
  R1 = Resistor [tolerance=±5% resistance=10k package=THT]

nets:
  N1: LED1.cathode, Arduino1.GND, R1.Pin_1
  N2: LED1.anode, Arduino1.D13/SCK
  N3: Arduino1.D2, S1.leg0, R1.Pin_0
  N4: Arduino1.5V, S1.leg1

notes:
  In this example, a pushbutton is used as a digital input and an LED is a digital output.
  Related example: http://arduino.cc/en/Tutorial/Button
