# Fritzing sketch CosmicRayGun (saved by Fritzing 1.0.0rc)
circuit board: 6.88566cm x 5.36311cm
breadboards: 2

parts:
  R6 = Resistor [resistance=220 tolerance=±5% power=0.25W package=THT]
  R5 = Resistor [resistance=220 tolerance=±5% power=0.25W package=THT]
  R4 = Resistor [resistance=220 tolerance=±5% power=0.25W package=THT]
  R3 = Resistor [resistance=220 tolerance=±5% power=0.25W package=THT]
  R2 = Resistor [resistance=220 tolerance=±5% power=0.25W package=THT]
  R1 = Resistor [resistance=220 tolerance=±5% power=0.25W package=THT]
  S2 = Pushbutton [package=THT]
  R7 = Resistor [resistance=1k tolerance=±5% power=0.25W package=THT]
  R8 = Resistor [resistance=1k tolerance=±5% power=0.25W package=THT]
  S1 = Pushbutton [package=THT]
  Speaker = Piezo Speaker
  LED5 = LED - 5mm [color="Red (633nm)" current=0.030A package="5 mm [THT]"]
  LED6 = LED - 5mm [color="Red (633nm)" current=0.030A package="5 mm [THT]"]
  LED3 = LED - 5mm [color="Yellow (585nm)" current=0.030A package="5 mm [THT]"]
  LED1 = LED - 5mm [color="Green (555nm)" current=0.030A package="5 mm [THT]"]
  LED4 = LED - 5mm [color="Yellow (585nm)" current=0.030A package="5 mm [THT]"]
  LED2 = LED - 5mm [color="Green (555nm)" current=0.030A package="5 mm [THT]"]
  PCB1 = Arduino Shield PCB  # not connected
  Arduino = Arduino Uno (Rev3)

nets:
  N1: R6.Pin_0, Arduino.D7
  N2: R6.Pin_1, LED1.anode
  N3: R5.Pin_0, Arduino.D8
  N4: R5.Pin_1, LED2.anode
  N5: R4.Pin_0, Arduino.D9_PWM
  N6: R4.Pin_1, LED3.anode
  N7: R3.Pin_0, Arduino.D10_PWM/SS
  N8: R3.Pin_1, LED4.anode
  N9: R2.Pin_0, Arduino.D11_PWM/MOSI
  N10: R2.Pin_1, LED5.anode
  N11: R1.Pin_0, Arduino.D12/MISO
  N12: R1.Pin_1, LED6.anode
  N13: S2.leg0, S1.leg1, Arduino.5V
  N14: S2.leg1, R7.Pin_1, Arduino.D5_PWM
  N15: R7.Pin_0, R8.Pin_0, LED5.cathode, LED6.cathode, LED3.cathode, LED1.cathode, LED4.cathode, LED2.cathode, Arduino.GND
  N16: R8.Pin_1, S1.leg0, Arduino.D13/SCK
  N17: Speaker.pin1, Arduino.D2
  N18: Speaker.pin2, Arduino.D3_PWM

notes:
  Get the code from the Fritzing Project Page:
  Cosmic Raygun

custom parts:
  Arduino Shield PCB: Plain PCB Shaped to fit an Arduino "Shield"
