# Fritzing sketch EDGY-motor-control-two-motors (saved by Fritzing 0.8.0b)
breadboards: 2

parts:
  EDGY_motor_control = EDGY
  M1 = DC Motor
  M2 = DC Motor
  Power_plug1 = Power plug
  Arduino1 = Arduino Uno (Rev3)

nets:
  N1: EDGY_motor_control.A1, Arduino1.D11_PWM/MOSI
  N2: EDGY_motor_control.B1, Arduino1.D10_PWM/SS
  N3: EDGY_motor_control.Speed1, Arduino1.D9_PWM
  VIN: EDGY_motor_control.Vin, Power_plug1.VCC
  N4: EDGY_motor_control.A2, Arduino1.D5_PWM
  N5: EDGY_motor_control.B2, Arduino1.D4
  N6: EDGY_motor_control.Speed2, Arduino1.D3_PWM
  N7: EDGY_motor_control.5V+, Arduino1.5V
  GND: EDGY_motor_control.GND, Power_plug1.GND, Arduino1.GND
  N8: EDGY_motor_control.B2out, M2.pin_2
  N9: EDGY_motor_control.A2out, M2.pin_1
  N10: EDGY_motor_control.B1out, M1.pin_2
  N11: EDGY_motor_control.A1out, M1.pin_1

// code stored in the sketch: EDGY-motor-control-two-motors.ino
int m1Pin = 5;
int m2Pin = 4;
int speed1Pin = 3;

int m1Pin2 = 5;
int m2Pin2 = 4;
int speed1Pin2 = 3;

void setup() {
  pinMode(m1Pin,OUTPUT);
  pinMode(m2Pin,OUTPUT);

  pinMode(m1Pin2,OUTPUT);
  pinMode(m2Pin2,OUTPUT);
}

void loop() {
for(int fadeValue = 0 ; fadeValue <= 255; fadeValue +=5) {
analogWrite(speed1Pin, fadeValue);
digitalWrite(m1Pin,HIGH);
digitalWrite(m2Pin,LOW);
delay(30);
}
delay(1000);
for(int fadeValue = 255 ; fadeValue >= 0; fadeValue -=5) {
analogWrite(speed1Pin, fadeValue);
digitalWrite(m2Pin,HIGH);
digitalWrite(m1Pin,LOW);
delay(30);
}
delay(1000);
for(int fadeValue = 0 ; fadeValue <= 255; fadeValue +=5) {
analogWrite(speed1Pin2, fadeValue);
digitalWrite(m1Pin2,HIGH);
digitalWrite(m2Pin2,LOW);
delay(30);
}
delay(1000);
for(int fadeValue = 255 ; fadeValue >= 0; fadeValue -=5) {
analogWrite(speed1Pin2, fadeValue);
digitalWrite(m2Pin2,HIGH);
digitalWrite(m1Pin2,LOW);
delay(30);
}
delay(1000);
}
