# Fritzing sketch Fading (saved by Fritzing 0.8.6b)
circuit board: 6.88566cm x 5.36311cm
breadboards: 2

parts:
  R1 = Resistor [tolerance=±5% resistance=220 package=THT]
  LED1 = LED - 5mm [color="Red (633nm)" package="5 mm [THT]"]
  Bauteil1 = Arduino Uno (Rev3)
  part = LED - 5mm [color="Red (633nm)" package="5 mm [THT]"]  # not connected

nets:
  N1: R1.Pin_0, Bauteil1.D9_PWM
  N2: R1.Pin_1, LED1.anode
  N3: LED1.cathode, Bauteil1.GND

notes:
  FADING

// code stored in the sketch: Fading.ino
/*
  Fading
  dimmt eine LED langsam an und aus
  
  Dieses Beispiel aus dem Fritzing Creator Kit: www.fritzing.org/creator-kit.
*/

int ledPin = 9;                                                   // ledPin wird deklariert

void setup(){ 
  // die analoge Ausgabe muss nicht im Setup initialisiert werden
} 

void loop(){ 
  for(int leuchtwert = 0; leuchtwert <= 255; leuchtwert++) {      // fadeValue wird in Fünferschritten hochgezählt 
    analogWrite(ledPin, leuchtwert);                              // und als analoger Wert an die LED übertragen 
    delay(2);                                                     // kurze Wartezeit                          
  } 
  for(int leuchtwert = 255; leuchtwert >= 0; leuchtwert--) {      // fadeValue wird in Fünferschritten runtergezählt 
    analogWrite(ledPin, leuchtwert);                              // und als analoger Wert an die LED übertragen 
    delay(2);                                                     // kurze Wartezeit                     
  } 
}
