# Fritzing sketch FlipFlop (saved by Fritzing 1.0.2b)
circuit board: 6.88566cm x 5.36311cm
breadboards: 2

parts:
  R3 = Resistor [tolerance=±5% resistance=100k power=0.25W package=THT]
  LED1 = LED - 5mm [color="Red (633nm)" current=0.030A package="5 mm [THT]"]
  LED2 = LED - 5mm [color="Green (555nm)" current=0.030A package="5 mm [THT]"]
  R1 = Resistor [tolerance=±5% resistance=220 power=0.25W package=THT]
  R2 = Resistor [tolerance=±5% resistance=220 power=0.25W package=THT]
  Button = Pushbutton [package=THT]
  Bauteil1 = Arduino Uno (Rev3)

nets:
  N1: R3.Pin_0, Button.leg1, Bauteil1.D2
  N2: R3.Pin_1, Bauteil1.5V
  N3: LED1.cathode, LED2.cathode, Button.leg0, Bauteil1.GND
  N4: LED1.anode, R1.Pin_1
  N5: LED2.anode, R2.Pin_1
  N6: R1.Pin_0, Bauteil1.D10_PWM/SS
  N7: R2.Pin_0, Bauteil1.D9_PWM

notes:
  FLIP FLOP

// code stored in the sketch: FlipFlop.ino
/*
  Flip Flop
  schaltet mittels eines Tasters zwischen zwei LEDs hin und her
  
  Dieses Beispiel aus dem Fritzing Creator Kit: www.fritzing.org/creator-kit.
*/

int tasterPin=2;                       // Pin an dem der Taster angeschlossen ist
int grueneLED=9;                       // Pin an dem die grüne LED angeschlossen ist
int roteLED=10;                        // Pin an dem die rote LED angeschlossen ist 

void setup(){
  pinMode(tasterPin, INPUT);           // Taster Pin wird als INPUT initialisiert
  pinMode(grueneLED, OUTPUT);          // LED Pin wird als OUTPUT initialisiert
  pinMode(roteLED, OUTPUT);            // LED Pin wird als OUTPUT initialisiert 
}

void loop(){
  if (digitalRead(tasterPin)==LOW){    // wenn der Taster gedrückt ist (LOW) 
    digitalWrite(grueneLED, HIGH);     // grüne LED einschalten
    digitalWrite(roteLED, LOW);        // rote LED abschalten
  } else {                             // sonst
    digitalWrite(grueneLED, LOW);      // grüne LED abschalten
    digitalWrite(roteLED, HIGH);       // rote LED einschalten
  }
}
