# Fritzing sketch H-Bridge (saved by Fritzing 0.9.1b)
circuit board: 6.88566cm x 5.36311cm
breadboards: 2

parts:
  L293D = L293D [package=THT]
  Motor2 = DC Motor
  VCC = Battery block 9V
  Motor1 = DC Motor
  PCB1 = Arduino Shield PCB  # not connected
  Bauteil1 = Arduino Uno (Rev3)

nets:
  N1: L293D.Enable_1, Bauteil1.D3_PWM
  N2: L293D.In_1, Bauteil1.D6_PWM
  N3: L293D.Out_1_(_Controlled_by_Enable_1_), Motor2.pin_2
  N4: L293D.0V, VCC.-, Bauteil1.GND
  N5: L293D.Out_2_(_Controlled_by_Enable_1_), Motor2.pin_1
  N6: L293D.In_2, Bauteil1.D5_PWM
  N7: L293D.+Vmotor, VCC.+, Bauteil1.VIN
  N8: L293D.Enable_2, Bauteil1.D9_PWM
  N9: L293D.In_3, Bauteil1.D11_PWM/MOSI
  N10: L293D.Out_3_(_Controlled_by_Enable_2_), Motor1.pin_2
  N11: L293D.Out_4_(_Controlled_by_Enable_2_), Motor1.pin_1
  N12: L293D.In_4, Bauteil1.D10_PWM/SS
  N13: L293D.+V, Bauteil1.5V

notes:
  H-BRIDGE

custom parts:
  Arduino Shield PCB: Plain PCB Shaped to fit an Arduino "Shield"

// code stored in the sketch: H-Bridge.ino
/*
  Motor
  dreht einen Motor erst rechts, dann links herum
  
  Dieses Beispiel aus dem Fritzing Creator Kit: www.fritzing.org/creator-kit.
*/

int motor_A=5;
int motor_B=4;
int motor_Speed=3;

void setup(){
  pinMode(motor_A,OUTPUT);
  pinMode(motor_B,OUTPUT);
}

void loop(){
  digitalWrite(motor_A,HIGH); 
  digitalWrite(motor_B,LOW);
  for (int i=0; i<256; i+=5){
    analogWrite(motor_Speed,i); 
    delay(20);
  }
  for (int i=255; i>0; i-=5){
    analogWrite(motor_Speed,i); 
    delay(20);
  }

  digitalWrite(motor_A,LOW); 
  digitalWrite(motor_B,HIGH);
  for (int i=0; i<256; i+=5){
    analogWrite(motor_Speed,i);
    delay(20);
  }
  for (int i=255; i>0; i-=5){
    analogWrite(motor_Speed,i);
    delay(20);
  }
}
