# Fritzing sketch Nachtlicht (saved by Fritzing 1.0.2b)
circuit board: 6.88566cm x 5.36311cm
breadboards: 2

parts:
  R1 = Resistor [tolerance=±5% resistance=220 power=0.25W package=THT]
  R2 = Resistor [tolerance=±5% resistance=220 power=0.25W package=THT]
  R3 = Resistor [tolerance=±5% resistance=220 power=0.25W package=THT]
  Bauteil1 = Arduino Uno (Rev3)
  LED2 = RGB LED (com. cathode, rbg) [color="Red (633nm)" current=0.030A package="5 mm [THT]"]
  R5 = Rotary Potentiometer (Small) [maximum_resistance=10kΩ knob_status=50% power=0.5W package=THT]

nets:
  N1: R1.Pin_0, Bauteil1.D11_PWM/MOSI
  N2: R1.Pin_1, LED2.red_anode
  N3: R2.Pin_0, Bauteil1.D10_PWM/SS
  N4: R2.Pin_1, LED2.blue_anode
  N5: R3.Pin_0, Bauteil1.D9_PWM
  N6: R3.Pin_1, LED2.green_anode
  N7: Bauteil1.A0, R5.wiper
  N8: Bauteil1.GND, LED2.common_cathode, R5.leg1
  N9: Bauteil1.5V, R5.leg2

notes:
  NACHTLICHT

// code stored in the sketch: Nachtlicht.ino
/*
  Nachtlicht
  blendet Farben durch
  
  Dieses Beispiel aus dem Fritzing Creator Kit: www.fritzing.org/creator-kit.
*/

int LEDGreen=9;                                      // LEDGreen Pins wird deklariert
int LEDBlue=10;                                      // LEDBlue Pins wird deklariert
int LEDRed=11;                                       // LEDRed Pins wird deklariert 

void setup(){
  pinMode(LEDRed,OUTPUT);                            // Pin wird als OUTPUT initialisiert
  pinMode(LEDGreen,OUTPUT);                          // Pin wird als OUTPUT initialisiert
  pinMode(LEDBlue,OUTPUT);                           // Pin wird als OUTPUT initialisiert
}

void loop(){
 for (int frame=0; frame<900; frame++){              // frame wird von 0 bis 900 hochgezählt
  if (frame<150) {                                   // wenn frame < 150  > rot
    analogWrite(LEDRed,255);                         // LED wird eingeschaltet
    analogWrite(LEDBlue,0);                          // LED wird abgeschaltet
    analogWrite(LEDGreen,0);                         // LED wird abgeschaltet
  } else if (frame<300) {                            // wenn frame < 300
    analogWrite(LEDRed,map(frame,150,300,255,0));    // LED wird ausgedimmt
    analogWrite(LEDBlue,map(frame,150,300,0,255));   // LED wird angedimmt 
    analogWrite(LEDGreen,0);                         // LED wird abgeschaltet
  } else if (frame<450) {                            // wenn frame < 450  > blau
    analogWrite(LEDRed,0);                           // LED wird abgeschaltet
    analogWrite(LEDBlue,255);                        // LED wird eingeschaltet
    analogWrite(LEDGreen,0);                         // LED wird abgeschaltet  
  } else if (frame<600) {                            // wenn frame < 600
    analogWrite(LEDRed,0);                           // LED wird abgeschaltet
    analogWrite(LEDBlue,map(frame,450,600,255,0));   // LED wird ausgedimmt 
    analogWrite(LEDGreen,map(frame,450,600,0,255));  // LED wird angedimmt
  } else if (frame<750) {                            // wenn frame < 750  > grün
    analogWrite(LEDRed,0);                           // LED wird abgeschaltet
    analogWrite(LEDBlue,0);                          // LED wird abgeschaltet 
    analogWrite(LEDGreen,255);                       // LED wird abgeschaltet
  } else if (frame<900) {                            // wenn frame < 900
    analogWrite(LEDRed,map(frame,750,900,0,255));    // LED wird angedimmt
    analogWrite(LEDBlue,0);                          // LED wird abgeschaltet 
    analogWrite(LEDGreen,map(frame,750,900,255,0));  // LED wird ausgedimmt
  }
  delay(10);                                         // kurze Pause
 }
}
