# Fritzing sketch ProcessingRGB (saved by Fritzing 0.9.1b)
circuit board: 6.88566cm x 5.36311cm
breadboards: 2

parts:
  R6 = Resistor [tolerance=±5% resistance=220 package=THT]
  R7 = Resistor [tolerance=±5% resistance=220 package=THT]
  R8 = Resistor [tolerance=±5% resistance=220 package=THT]
  LED1 = RGB LED (com. cathode, rbg) [package="5 mm [THT]"]
  PCB1 = Arduino Shield PCB  # not connected
  R1 = Rotary Potentiometer (Small) [maximum_resistance=100kΩ package=THT]
  Bauteil1 = Arduino Uno (Rev3)

nets:
  N1: R6.Pin_0, Bauteil1.D9_PWM
  N2: R6.Pin_1, LED1.red_anode
  N3: R7.Pin_0, Bauteil1.D10_PWM/SS
  N4: R7.Pin_1, LED1.blue_anode
  N5: R8.Pin_0, Bauteil1.D11_PWM/MOSI
  N6: R8.Pin_1, LED1.green_anode
  N7: LED1.common_cathode, R1.leg1, Bauteil1.GND
  N8: R1.wiper, Bauteil1.A0
  N9: R1.leg2, Bauteil1.5V

notes:
  PROCESSING-RGB

custom parts:
  Arduino Shield PCB: Plain PCB Shaped to fit an Arduino "Shield"

// code stored in the sketch: ProcessingRGB.ino
/*
 
  Processing RGB
  
  Starte hierf?r die Arduino-Software und lade das Programm 
  Datei > Beispiele > Firmata > Standard Firmata

*/
