# Fritzing sketch Servo (saved by Fritzing 0.8.6b)
circuit board: 6.88566cm x 5.36311cm
breadboards: 2

parts:
  Servo = Basic Servo
  Potentiometer = Rotary Potentiometer (Small) [maximum_resistance=100kΩ package=THT]
  Bauteil1 = Arduino Uno (Rev3)

nets:
  GND: Servo.gnd, Potentiometer.leg1, Bauteil1.GND
  VCC: Servo.vcc, Potentiometer.leg2, Bauteil1.5V
  N1: Servo.pulse, Bauteil1.D9_PWM
  N2: Potentiometer.wiper, Bauteil1.A0

notes:
  Orange
  Rot
  Braun
  SERVO

// code stored in the sketch: Servo.ino
/*
  Servo
  ein Potentiometer steuert die Position eines Servos
  
  Dieses Beispiel aus dem Fritzing Creator Kit: www.fritzing.org/creator-kit.
*/

#include <Servo.h>                   // einbinden der Servo Bibliothek (library)
 
Servo myservo;                       // erzeugt ein Servo-Objekt
int potpin = 0 ;                     // Potentiometer-Pin wird deklariert
int val;                             // val speichert den Wert des Potentiometers zwischen
 
void setup() 
{ 
  myservo.attach(9);                  // verbindet das Servoobjekt an Pin 9
} 
 
void loop() 
{ 
  val = analogRead(potpin);            // Potentiometer-Wert wird ausgelesen
  val = map(val, 0, 1023, 0, 179);     // und in den Wertebereich von 0 bis 179 überführt
  myservo.write(val);                  // stellt den Servo auf den Wert val
  delay(15);                           // wartet, damit sich der Servo drehen kann
}
