# Fritzing sketch Synthesizer (saved by Fritzing 1.0.0rc)
circuit board: 6.88566cm x 5.36311cm
breadboards: 2

parts:
  R3 = Resistor [tolerance=±5% resistance=220 power=0.25W package=THT]
  SG1 = Buzzer 12mm [package=buzzer-12mm-ns]
  R1 = Rotary Potentiometer (Small) [maximum_resistance=100kΩ knob_status=50% power=0.5W package=THT]
  R2 = Rotary Potentiometer (Small) [maximum_resistance=100kΩ knob_status=50% power=0.5W package=THT]
  Arduino1 = Arduino Uno (Rev3)

nets:
  N1: R3.Pin_0, SG1.1
  N2: R3.Pin_1, R1.leg1, R2.leg1, Arduino1.GND
  N3: SG1.2, Arduino1.D8
  N4: R1.wiper, Arduino1.A1
  N5: R1.leg2, R2.leg2, Arduino1.5V
  N6: R2.wiper, Arduino1.A0

notes:
  SYNTHESIZER

custom parts:
  Buzzer 12mm: Buzzer 12mm Spark Fun Electronics SKU : Comp-Buzzer

// code stored in the sketch: Synthesizer.ino
/*
  Synthesizer
  erzeugt eine Frequenzschema aus den Werten zweier Potientiometer
  
  Dieses Beispiel aus dem Fritzing Creator Kit: www.fritzing.org/creator-kit.
*/

int buzzerPin = 8;                             // deklariert den Pin des Piezos
int potPin1 = 0;                               // Potentiometer 0 Pin
int potPin2 = 1;                               // Potentiometer 1 Pin

int toneHeight;                                // speichert die Tonhöhe zwischen
int lfo;                                       // speichert die Frequensgeschwindigkeit

/* lfo bezeichnet einen "niederfrequenten Oszillator" - also eine zeitliche Frequenzänderung */

void setup() {
  pinMode(buzzerPin, OUTPUT);                  // buzzerPin wird als OUTPUT deklariert
}

void play(int myToneHeight) {                  // play-Methode
    digitalWrite(buzzerPin, HIGH);             // Piezo wird angeschalten
    delayMicroseconds(myToneHeight);           // Wartezeit wird durch toneHeight beeinflusst
    digitalWrite(buzzerPin, LOW);              // Piezo wird abgeschalten
    delayMicroseconds(myToneHeight);           // Wartezeit wird durch toneHeight beeinflusst
}

void loop() {
  toneHeight=analogRead(potPin1);              // Tonhöhe ist Wert vom Potentiometer 1
  lfo=analogRead(potPin2);                     // lfo ist Wert vom Potentiometer 1
  
  for (int i = (lfo/10); i > 0; i--) {         // Tonhöhe steigend in Abhängigkeit des lfo Wertes
    play(toneHeight);
  }
  delayMicroseconds(lfo);                      // Pause
  for (int i = 0; i < lfo/10; i++) {           // Tonhöhe sinkend in Abhängigkeit des lfo Wertes
    play(toneHeight);
  }
}
