# Fritzing sketch TwitterSaurus (saved by Fritzing 0.9.1b)
circuit board: 6.88566cm x 5.36311cm
breadboards: 2

parts:
  Servo = Basic Servo
  PCB1 = Arduino Shield PCB  # not connected
  Bauteil1 = Arduino Uno (Rev3)

nets:
  GND: Servo.gnd, Bauteil1.GND
  VCC: Servo.vcc, Bauteil1.5V
  N1: Servo.pulse, Bauteil1.D9_PWM

notes:
  TWITTER-SAURUS

custom parts:
  Arduino Shield PCB: Plain PCB Shaped to fit an Arduino "Shield"

// code stored in the sketch: Twittersaurus.ino
/*
 
  Twittersaurus
  
  Starte hierf?r die Arduino-Software und lade das Programm 
  Datei > Beispiele > Firmata > Standard Firmata

*/
