# Fritzing sketch Verstaerkung (saved by Fritzing 0.9.1b)
circuit board: 6.88566cm x 5.36311cm
breadboards: 2

parts:
  Motor = DC Motor
  Batterie = Battery block 9V
  FET = Basic FET N-Channel [package="TO220 [THT]"]
  PCB1 = Arduino Shield PCB  # not connected
  Arduino1 = Arduino Uno (Rev3)

nets:
  N1: Motor.pin_1, FET.drain
  N2: Motor.pin_2, Batterie.+
  N3: Batterie.-, FET.source, Arduino1.GND
  N4: FET.gate, Arduino1.D9_PWM

notes:
  +
  -
  VERSTAERKUNG

custom parts:
  Arduino Shield PCB: Plain PCB Shaped to fit an Arduino "Shield"

// code stored in the sketch: Verstaerkung.ino
/*
  Verstärkung
  fährt einen Motor langsam hoch und wieder runter
  
  Dieses Beispiel ist aus dem Fritzing Creator Kit: www.fritzing.org/creator-kit.
*/

int motorPin = 9;                                                   // ledPin wird deklariert

void setup(){ 
  // die analoge Ausgabe muss nicht im Setup initialisiert werden
} 

void loop(){ 
  for(int drehzahl = 0; drehzahl <= 255; drehzahl++) {      // drehzahl wird in Fünferschritten hochgezählt 
    analogWrite(motorPin, drehzahl);                              // und als analoger Wert an den Motor übertragen 
    delay(2);                                                     // kurze Wartezeit                          
  } 
  for(int drehzahl = 255; drehzahl >= 0; drehzahl--) {      // drehzahl wird in Fünferschritten runtergezählt 
    analogWrite(motorPin, drehzahl);                              // und als analoger Wert an den Motor übertragen 
    delay(2);                                                     // kurze Wartezeit                     
  } 
}
