# Fritzing sketch Zaubertafel (saved by Fritzing 0.9.1b)
circuit board: 6.88566cm x 5.36311cm
breadboards: 2

parts:
  S1 = Tilt Switch [package=THT]
  R6 = Resistor [tolerance=±5% resistance=100k package=THT]
  R5 = Rotary Potentiometer (Small) [maximum_resistance=100kΩ package=THT]
  R4 = Rotary Potentiometer (Small) [maximum_resistance=100kΩ package=THT]
  PCB1 = Arduino Shield PCB  # not connected
  Bauteil1 = Arduino Uno (Rev3)

nets:
  N1: S1.Pin_1, R5.leg1, R4.leg1, Bauteil1.GND
  N2: S1.Pin_2, R6.Pin_0, Bauteil1.D2
  N3: R6.Pin_1, R5.leg2, R4.leg2, Bauteil1.5V
  N4: R5.wiper, Bauteil1.A1
  N5: R4.wiper, Bauteil1.A0

notes:
  ZAUBERTAFEL

custom parts:
  Arduino Shield PCB: Plain PCB Shaped to fit an Arduino "Shield"

// code stored in the sketch: Zaubertafel.ino
/*
 
  Zaubertafel
  
  Starte hierfür die Arduino-Software und lade das Programm 
  Datei > Beispiele > Firmata > Standard Firmata

*/
