# Fritzing sketch Fading (saved by Fritzing 0.8.6b)
circuit board: 6.88566cm x 5.36311cm
breadboards: 2

parts:
  R1 = Resistor [tolerance=±5% resistance=220 package=THT]
  LED1 = LED - 5mm [color="Red (633nm)" package="5 mm [THT]"]
  Bauteil1 = Arduino Uno (Rev3)
  part = LED - 5mm [color="Red (633nm)" package="5 mm [THT]"]  # not connected

nets:
  N1: R1.Pin_0, Bauteil1.D9_PWM
  N2: R1.Pin_1, LED1.anode
  N3: LED1.cathode, Bauteil1.GND

notes:
  FADING

// code stored in the sketch: Fading.ino
/*
  Fading
  fading an LED slowly on and off again
  
  This example is part of the Fritzing Creator Kit: www.fritzing.org/creator-kit.
*/

int ledPin = 9;                                                   // ledPin is declared

void setup(){ 
  // no need to declare the analog output in the setup 
} 

void loop(){ 
  for(int fadeValue = 0; fadeValue <= 255; fadeValue += 5) {      // fadeValue is counted up in steps of five
    analogWrite(ledPin, fadeValue);                               // and sent to the led as an analog value
    delay(2);                                                     // short stop                        
  } 
  for(int fadeValue = 255; fadeValue >= 0; fadeValue -= 5) {      // fadeValue is counted down in steps of five
    analogWrite(ledPin, fadeValue);                               // and sent to the led as an analog value 
    delay(2);                                                     // short stop                         
  } 
}
