# Fritzing sketch Fortuneteller (saved by Fritzing 1.0.0d)
circuit board: 6.88566cm x 5.36311cm
breadboards: 2

parts:
  R1 = Resistor [tolerance=±5% resistance=100k power=0.25W package=THT]
  Tilt = Tilt Switch [package=THT]
  PCB1 = Arduino Shield PCB  # not connected
  Warte_noch_etwas_damit = LED - 5mm [color="Yellow (585nm)" current=0.030A package="5 mm [THT]"]
  R4 = Resistor [tolerance=±5% resistance=220 power=0.25W package=THT]
  Ja_aber_mit_Stil! = LED - 5mm [color="Blue (505nm)" current=0.030A package="5 mm [THT]"]
  Nein_lieber_nicht = LED - 5mm [color="Red (633nm)" current=0.030A package="5 mm [THT]"]
  R5 = Resistor [tolerance=±5% resistance=220 power=0.25W package=THT]
  R6 = Resistor [tolerance=±5% resistance=220 power=0.25W package=THT]
  R2 = Resistor [tolerance=±5% resistance=220 power=0.25W package=THT]
  Folge_deinem_Herzen = LED - 5mm [color="Green (555nm)" current=0.030A package="5 mm [THT]"]
  R3 = Resistor [tolerance=±5% resistance=220 power=0.25W package=THT]
  Unbedingt!_Sofort! = LED - 5mm [color="Blue (505nm)" current=0.030A package="5 mm [THT]"]
  Arduino1 = Arduino Uno (Rev3)

nets:
  N1: R1.Pin_0, Tilt.Pin_2, Arduino1.D3_PWM
  N2: R1.Pin_1, Arduino1.5V
  N3: Tilt.Pin_1, Warte_noch_etwas_damit.cathode, Ja_aber_mit_Stil!.cathode, Nein_lieber_nicht.cathode, Folge_deinem_Herzen.cathode, Unbedingt!_Sofort!.cathode, Arduino1.GND
  N4: Warte_noch_etwas_damit.anode, R5.Pin_0
  N5: R4.Pin_0, Folge_deinem_Herzen.anode
  N6: R4.Pin_1, Arduino1.D10_PWM/SS
  N7: Ja_aber_mit_Stil!.anode, R2.Pin_0
  N8: Nein_lieber_nicht.anode, R3.Pin_0
  N9: R5.Pin_1, Arduino1.D9_PWM
  N10: R6.Pin_0, Unbedingt!_Sofort!.anode
  N11: R6.Pin_1, Arduino1.D8
  N12: R2.Pin_1, Arduino1.D12/MISO
  N13: R3.Pin_1, Arduino1.D11_PWM/MOSI

notes:
  FORTUNETELLER

custom parts:
  Arduino Shield PCB: Plain PCB Shaped to fit an Arduino "Shield"

// code stored in the sketch: Fortuneteller.ino
/*
  fortune teller
  switching between five LEDs to tell the future
  
  This example is part of the Fritzing Creator Kit: www.fritzing.org/creatorkit.
*/

int pins[] = {8,9,10,11,12};            // the pins of the LEDs are stored in an array
int tiltPin = 3;                        // pin number where the tilt switch is attached

void setup() {                           
  for (int i=0; i<5; i=i+1){            
    pinMode(pins[i] , OUTPUT);          // LED pins are declared as outputs
  }
  pinMode(tiltPin,INPUT);               // pin of the tilt switch is declared as input
  randomSeed(analogRead(0));            // initialize random number generator based on random state of pin zero
}

void loop() {
  if (digitalRead(tiltPin)==HIGH){      // when the tilt switch is open
   for (int i=0; i<5; i=i+1){           // all the LEDs
     digitalWrite(pins[i],LOW);         // get switched off
   }                                    // 
   int myRandom=random(0,5);            // a random LED 
   digitalWrite(pins[myRandom],HIGH);   // is switched on
   delay(20);                           // the program is waiting to breath
  }
}
