# Fritzing sketch Magic_Board (saved by Fritzing 0.8.4b)
circuit board: 6.88566cm x 5.36311cm
breadboards: 2

parts:
  S1 = Tilt Switch [package=THT]
  R6 = Resistor [tolerance=±5% resistance=100k package=THT]
  Component1 = Arduino Uno (Rev3)
  R5 = Rotary Potentiometer (Small) [maximum_resistance=100kΩ package=THT]
  R4 = Rotary Potentiometer (Small) [maximum_resistance=100kΩ package=THT]

nets:
  N1: S1.Pin_1, Component1.GND, R5.leg1, R4.leg1
  N2: S1.Pin_2, R6.Pin_0, Component1.D2
  N3: R6.Pin_1, Component1.5V, R5.leg2, R4.leg2
  N4: Component1.A0, R4.wiper
  N5: Component1.A1, R5.wiper

notes:
  MAGIC BOARD
