# Fritzing sketch NightLight (saved by Fritzing 1.0.2b)
circuit board: 6.88566cm x 5.36311cm
breadboards: 2

parts:
  R1 = Resistor [tolerance=±5% resistance=220 power=0.25W package=THT]
  R2 = Resistor [tolerance=±5% resistance=220 power=0.25W package=THT]
  R3 = Resistor [tolerance=±5% resistance=220 power=0.25W package=THT]
  LED2 = RGB LED (com. cathode, rbg) [color="Red (633nm)" current=0.030A package="5 mm [THT]"]
  R4 = Rotary Potentiometer (Small) [maximum_resistance=100kΩ knob_status=50% power=0.5W package=THT]
  Bauteil1 = Arduino Uno (Rev3)

nets:
  N1: R1.Pin_0, Bauteil1.D11_PWM/MOSI
  N2: R1.Pin_1, LED2.red_anode
  N3: R2.Pin_0, Bauteil1.D10_PWM/SS
  N4: R2.Pin_1, LED2.blue_anode
  N5: R3.Pin_0, Bauteil1.D9_PWM
  N6: R3.Pin_1, LED2.green_anode
  N7: LED2.common_cathode, R4.leg1, Bauteil1.GND
  N8: R4.wiper, Bauteil1.A0
  N9: R4.leg2, Bauteil1.5V

notes:
  NIGHT_LIGHT

// code stored in the sketch: NightLight.ino
/*
  night light
  fading through the colors of a rainbow
  
  This example is part of the Fritzing Creator Kit: www.fritzing.org/creatorkit.
*/

int LEDGreen=9;                                      // LEDGreen pin declared
int LEDBlue=10;                                      // LEDBlue pin declared
int LEDRed=11;                                       // LEDRed pin declared

void setup(){
  pinMode(LEDRed,OUTPUT);                            // pin is output
  pinMode(LEDGreen,OUTPUT);                          // pin is output
  pinMode(LEDBlue,OUTPUT);                           // pin is output
}

void loop(){
 for (int frame=0; frame<900; frame++){              // frame is counted up from 0 to 900 
  if (frame<150) {                                   // if frame < 150  => red
    analogWrite(LEDRed,255);                         // LED switched on
    analogWrite(LEDBlue,0);                          // switch off LED
    analogWrite(LEDGreen,0);                         // switch off LED
  } else if (frame<300) {                            // if frame < 300
    analogWrite(LEDRed,map(frame,150,300,255,0));    // fade off LED
    analogWrite(LEDBlue,map(frame,150,300,0,255));   // fade on LED 
    analogWrite(LEDGreen,0);                         // switch off LED
  } else if (frame<450) {                            // if frame < 450  => blue
    analogWrite(LEDRed,0);                           // switch off LED
    analogWrite(LEDBlue,255);                        // switch on LED
    analogWrite(LEDGreen,0);                         // switch off LED  
  } else if (frame<600) {                            // if frame < 600
    analogWrite(LEDRed,0);                           // switch off LED
    analogWrite(LEDBlue,map(frame,450,600,255,0));   // fade off LED 
    analogWrite(LEDGreen,map(frame,450,600,0,255));  // fade on LED
  } else if (frame<750) {                            // if frame < 750  => green
    analogWrite(LEDRed,0);                           // switch off LED
    analogWrite(LEDBlue,0);                          // switch off LED 
    analogWrite(LEDGreen,255);                       // switch off LED
  } else if (frame<900) {                            // if frame < 900
    analogWrite(LEDRed,map(frame,750,900,0,255));    // fade on LED
    analogWrite(LEDBlue,0);                          // switch off LED 
    analogWrite(LEDGreen,map(frame,750,900,255,0));  // fade off LED
  }
  delay(10);                                         // short break
 }
}
