# Fritzing sketch Night_Light (saved by Fritzing 0.8.4b)
circuit board: 6.88566cm x 5.36311cm
breadboards: 2

parts:
  R1 = Resistor [tolerance=±5% resistance=220 package=THT]
  R2 = Resistor [tolerance=±5% resistance=220 package=THT]
  R3 = Resistor [tolerance=±5% resistance=220 package=THT]
  Component1 = Arduino Uno (Rev3)
  LED2 = RGB LED (com. cathode, rbg) [package="5 mm [THT]"]
  R4 = Rotary Potentiometer (Small) [maximum_resistance=100kΩ package=THT]

nets:
  N1: R1.Pin_0, Component1.D11_PWM/MOSI
  N2: R1.Pin_1, LED2.red_anode
  N3: R2.Pin_0, Component1.D10_PWM/SS
  N4: R2.Pin_1, LED2.blue_anode
  N5: R3.Pin_0, Component1.D9_PWM
  N6: R3.Pin_1, LED2.green_anode
  N7: Component1.A0, R4.wiper
  N8: Component1.GND, LED2.common_cathode, R4.leg1
  N9: Component1.5V, R4.leg2

notes:
  NIGHT LIGHT
