# Fritzing sketch Potentiometer (saved by Fritzing 0.8.4b)
circuit board: 6.88566cm x 5.36311cm
breadboards: 2

parts:
  LED1 = LED - 5mm [color="Red (633nm)" package="5 mm [THT]"]
  R1 = Resistor [tolerance=±5% resistance=220 package=THT]
  R2 = Resistor [tolerance=±5% resistance=220 package=THT]
  LED2 = LED - 5mm [color="Green (555nm)" package="5 mm [THT]"]
  Arduino1 = Arduino Uno (Rev3)
  R6 = Rotary Potentiometer (Small) [maximum_resistance=100kΩ package=THT]

nets:
  N1: LED1.cathode, R1.Pin_0
  N2: LED1.anode, Arduino1.D6_PWM
  N3: R1.Pin_1, R2.Pin_1, Arduino1.GND, R6.leg1
  N4: R2.Pin_0, LED2.cathode
  N5: LED2.anode, Arduino1.D5_PWM
  N6: Arduino1.A0, R6.wiper
  N7: Arduino1.5V, R6.leg2

notes:
  POTENTIOMETER
