# Fritzing sketch Processing_RGB (saved by Fritzing 0.8.4b)
circuit board: 6.88566cm x 5.36311cm
breadboards: 2

parts:
  R6 = Resistor [tolerance=±5% resistance=220 package=THT]
  R7 = Resistor [tolerance=±5% resistance=220 package=THT]
  R8 = Resistor [tolerance=±5% resistance=220 package=THT]
  Component1 = Arduino Uno (Rev3)
  LED1 = RGB LED (com. cathode, rbg) [package="5 mm [THT]"]
  R1 = Rotary Potentiometer (Small) [maximum_resistance=100kΩ package=THT]

nets:
  N1: R6.Pin_0, Component1.D9_PWM
  N2: R6.Pin_1, LED1.red_anode
  N3: R7.Pin_0, Component1.D10_PWM/SS
  N4: R7.Pin_1, LED1.blue_anode
  N5: R8.Pin_0, Component1.D11_PWM/MOSI
  N6: R8.Pin_1, LED1.green_anode
  N7: Component1.A0, R1.wiper
  N8: Component1.GND, LED1.common_cathode, R1.leg1
  N9: Component1.5V, R1.leg2

notes:
  PROCESSING RGB
