# Fritzing sketch Servo (saved by Fritzing 0.8.6b)
circuit board: 6.88566cm x 5.36311cm
breadboards: 2

parts:
  Servo = Basic Servo
  Potentiometer = Rotary Potentiometer (Small) [maximum_resistance=100kΩ package=THT]
  Bauteil1 = Arduino Uno (Rev3)

nets:
  GND: Servo.gnd, Potentiometer.leg1, Bauteil1.GND
  VCC: Servo.vcc, Potentiometer.leg2, Bauteil1.5V
  N1: Servo.pulse, Bauteil1.D9_PWM
  N2: Potentiometer.wiper, Bauteil1.A0

notes:
  orange
  red
  brown
  SERVO

// code stored in the sketch: Servo.ino
/*
  Servo
  a potentiometer controls the position of a servo
  
  This example is part of the Fritzing Creator Kit: www.fritzing.org/creator-kit.
*/

#include <Servo.h>                   // include the library Servo.h
 
Servo myservo;                       // creates a servo object
int potpin = 0 ;                     // potentiometer pin declaration
int val;                             // val stores the position of the potentiometer
 
void setup() 
{ 
  myservo.attach(9);                  // connects a servo object to pin 9
} 
 
void loop() 
{ 
  val = analogRead(potpin);            // potentiometer value is read out
  val = map(val, 0, 1023, 0, 179);     // and mapped to the range 0 to 179
  myservo.write(val);                  // turning the servo to the angle in val
  delay(15);                           // give the servo time to react
}
