# Fritzing sketch Synthesizer (saved by Fritzing 1.0.0rc)
circuit board: 6.88566cm x 5.36311cm
breadboards: 2

parts:
  R3 = Resistor [tolerance=±5% resistance=220 power=0.25W package=THT]
  SG1 = Buzzer 12mm [package=buzzer-12mm-ns]
  R1 = Rotary Potentiometer (Small) [maximum_resistance=100kΩ knob_status=50% power=0.5W package=THT]
  R2 = Rotary Potentiometer (Small) [maximum_resistance=100kΩ knob_status=50% power=0.5W package=THT]
  Arduino1 = Arduino Uno (Rev3)

nets:
  N1: R3.Pin_0, SG1.1
  N2: R3.Pin_1, R1.leg1, R2.leg1, Arduino1.GND
  N3: SG1.2, Arduino1.D8
  N4: R1.wiper, Arduino1.A1
  N5: R1.leg2, R2.leg2, Arduino1.5V
  N6: R2.wiper, Arduino1.A0

notes:
  SYNTHESIZER

custom parts:
  Buzzer 12mm: Buzzer 12mm Spark Fun Electronics SKU : Comp-Buzzer

// code stored in the sketch: Synthesizer.ino
/*
  Synthesizer
  creating sound from electronics
  
  This example is part of the Fritzing Creator Kit: www.fritzing.org/creator-kit.
*/

int buzzerPin = 8;                             // piezo pin declaration
int potPin1 = 0;                               // potentiometer 1 pin declaration
int potPin2 = 1;                               // potentiometer 2 pin declaration

int toneHeight;                                // store the tone height
int lfo;                                       // store the frequency speed

/* lfo is a "low frequency oscillator" - so a frequency change depending on time */

void setup() {
  pinMode(buzzerPin, OUTPUT);                  // buzzerPin as output
}

void play(int myToneHeight) {                  // play method
    digitalWrite(buzzerPin, HIGH);             // piezo is switched on
    delayMicroseconds(myToneHeight);           // stopping time influenced by toneHeight 
    digitalWrite(buzzerPin, LOW);              // piezo is switched off
    delayMicroseconds(myToneHeight);           // stopping time influenced by toneHeight 
}

void loop() {
  toneHeight=analogRead(potPin1);              // toneheight is value of potentiometer 1
  lfo=analogRead(potPin2);                     // lfo is value of potentiometer 2
  
  for (int i = (lfo/10); i > 0; i--) {         // toneheight rising depending on lfo
    play(toneHeight);                          // execute play method
  }
  delayMicroseconds(lfo);                      // break
  for (int i = 0; i < lfo/10; i++) {           // toneheight sinking depending on lfo
    play(toneHeight);                          // execute play method
  }
}
