# Fritzing sketch Twitter_Saurus (saved by Fritzing 0.8.4b)
circuit board: 6.88566cm x 5.36311cm
breadboards: 2

parts:
  Servo = Basic Servo
  Component1 = Arduino Uno (Rev3)

nets:
  GND: Servo.gnd, Component1.GND
  VCC: Servo.vcc, Component1.5V
  N1: Servo.pulse, Component1.D9_PWM

notes:
  TWITTER SAURUS
