# Fritzing sketch Workshop_04_Fade-LED (saved by Fritzing 1.0.2b)
circuit board: 6.88566cm x 5.36311cm
breadboards: 2

parts:
  R3 = Resistor [tolerance=±5% resistance=100k power=0.25W package=THT]
  LED1 = LED - 5mm [color="Red (633nm)" current=0.030A package="5 mm [THT]"]
  LED2 = LED - 5mm [color="Green (555nm)" current=0.030A package="5 mm [THT]"]
  R1 = Resistor [tolerance=±5% resistance=220 power=0.25W package=THT]
  R2 = Resistor [tolerance=±5% resistance=220 power=0.25W package=THT]
  Button = Pushbutton [package=THT]
  PCB1 = Arduino Shield PCB  # not connected
  Bauteil1 = Arduino Uno (Rev3)

nets:
  N1: R3.Pin_0, Button.leg1, Bauteil1.D2
  N2: R3.Pin_1, Bauteil1.5V
  N3: LED1.cathode, LED2.cathode, Button.leg0, Bauteil1.GND
  N4: LED1.anode, R1.Pin_1
  N5: LED2.anode, R2.Pin_1
  N6: R1.Pin_0, Bauteil1.D10_PWM/SS
  N7: R2.Pin_0, Bauteil1.D9_PWM

notes:
  FLIP FLOP

custom parts:
  Arduino Shield PCB: Plain PCB Shaped to fit an Arduino "Shield"

// code stored in the sketch: FlipFlop.ino
/*
  Flip Flop
  switching between two LEDs using a button
  
  This example is part of the Fritzing Creator Kit: www.fritzing.org/creator-kit.
*/

int buttonPin=2;                       // Pin where the button is attached
int greenLED=9;                        // Pin where the green LED is attached
int redLED=10;                         // Pin where the red LED is attached 

void setup(){
  pinMode(buttonPin, INPUT);           // button is initialised as INPUT 
  pinMode(greenLED, OUTPUT);           // green LED pin is initialised as OUTPUT 
  pinMode(redLED, OUTPUT);             // red LED pin is initialised as OUTPUT  
}

void loop(){
  if (digitalRead(buttonPin)==LOW){    // if the button is pressed (LOW) 
    digitalWrite(greenLED, HIGH);      // switch on green LED
    digitalWrite(redLED, LOW);         // switch off red LED
  } else {                             // else (if button is not pressed)
    digitalWrite(greenLED, LOW);       // switch off green LED
    digitalWrite(redLED, HIGH);        // switch on red LED
  }
}

// code stored in the sketch: Workshop_03_FlipFlop-w-Button.ino
int buttonPin=2;
int greenLED=9;
int redLED=10;

void setup(){
  pinMode(buttonPin, INPUT);
  pinMode(greenLED, OUTPUT);
  pinMode(redLED, OUTPUT);
}
void loop(){
  if (digitalRead(buttonPin)==LOW){
    digitalWrite(greenLED, HIGH);
    digitalWrite(redLED, LOW);
  } 
  else {
    digitalWrite(greenLED, LOW);
    digitalWrite(redLED, HIGH);
  }
}

// code stored in the sketch: Workshop_04_Fade-LED.ino
int ledPin = 9;

void setup()  {
  pinMode(ledPin, OUTPUT);
}
void loop(){
  for (int lightValue=0; lightValue<=255; lightValue++){
    analogWrite(ledPin, lightValue);
    delay(2); 
  }
  for (int lightValue=255; lightValue>=0; lightValue--){
    analogWrite(ledPin, lightValue);
    delay(2);
  } 
}
