# Fritzing sketch Workshop_06_Automatic-Lightning (saved by Fritzing 1.0.0rc)
circuit board: 6.88566cm x 5.36311cm
breadboards: 2

parts:
  R1 = Resistor [tolerance=±5% resistance=220 power=0.25W package=THT]
  R2 = Resistor [tolerance=±5% resistance=220 power=0.25W package=THT]
  PCB1 = Arduino Shield PCB  # not connected
  Bauteil1 = Arduino Uno (Rev3)
  R4 = Resistor [tolerance=±5% resistance=10k power=0.25W package=THT]
  R5 = Photocell (LDR) [power=0.25W dark_resistance_@0.01lx=300kΩ light_resistance_@100lx=400Ω luminance=10lx package=THT]
  LED1 = LED - 5mm [color="White (4500K)" current=0.030A package="5 mm [THT]"]
  LED2 = LED - 5mm [color="White (4500K)" current=0.030A package="5 mm [THT]"]

nets:
  N1: R1.Pin_0, Bauteil1.D10_PWM/SS
  N2: R1.Pin_1, LED1.anode
  N3: R2.Pin_0, Bauteil1.D9_PWM
  N4: R2.Pin_1, LED2.anode
  N5: Bauteil1.A0, R4.Pin_1, R5.pin_0
  N6: Bauteil1.GND, R5.pin_1, LED1.cathode, LED2.cathode
  N7: Bauteil1.5V, R4.Pin_0

notes:
  FLIP FLOP

custom parts:
  Arduino Shield PCB: Plain PCB Shaped to fit an Arduino "Shield"

// code stored in the sketch: FlipFlop.ino
/*
  Flip Flop
  switching between two LEDs using a button
  
  This example is part of the Fritzing Creator Kit: www.fritzing.org/creator-kit.
*/

int buttonPin=2;                       // Pin where the button is attached
int greenLED=9;                        // Pin where the green LED is attached
int redLED=10;                         // Pin where the red LED is attached 

void setup(){
  pinMode(buttonPin, INPUT);           // button is initialised as INPUT 
  pinMode(greenLED, OUTPUT);           // green LED pin is initialised as OUTPUT 
  pinMode(redLED, OUTPUT);             // red LED pin is initialised as OUTPUT  
}

void loop(){
  if (digitalRead(buttonPin)==LOW){    // if the button is pressed (LOW) 
    digitalWrite(greenLED, HIGH);      // switch on green LED
    digitalWrite(redLED, LOW);         // switch off red LED
  } else {                             // else (if button is not pressed)
    digitalWrite(greenLED, LOW);       // switch off green LED
    digitalWrite(redLED, HIGH);        // switch on red LED
  }
}

// code stored in the sketch: Workshop_06_Automatic-Lightning.ino
int lightsensorPin = 0;
int headlightsPin1 = 9;
int headlightsPin2 = 10;
int switchingthreshold= 300;
int wait = 1000;
long timer = 0;
int value;

void setup(){
  //Serial.begin(9600);
  pinMode(headlightsPin1,OUTPUT);
  pinMode(headlightsPin2,OUTPUT);
}

void loop(){
  value = analogRead(lightsensorPin);
  //Serial.println(value);
  
  if (value<switchingthreshold){
    timer=millis();
    digitalWrite(headlightsPin1, HIGH);
    digitalWrite(headlightsPin2, HIGH);
  } 
  else if (millis()>wait+timer){
    digitalWrite(headlightsPin1, LOW);
    digitalWrite(headlightsPin2, LOW);    
  }
  
  delay(15); 
}
