# Fritzing sketch Workshop_07_Servo (saved by Fritzing 1.0.0d)
circuit board: 6.88566cm x 5.36311cm
breadboards: 2

parts:
  LED1 = LED - 5mm [color="White (4500K)" current=0.030A package="5 mm [THT]"]
  LED2 = LED - 5mm [color="White (4500K)" current=0.030A package="5 mm [THT]"]
  R1 = Resistor [tolerance=±5% resistance=220 power=0.25W package=THT]
  R2 = Resistor [tolerance=±5% resistance=220 power=0.25W package=THT]
  Bauteil1 = Arduino Uno (Rev3)
  R4 = Resistor [tolerance=±5% resistance=10k power=0.25W package=THT]
  R5 = Photocell (LDR) [power=0.25W dark_resistance_@0.01lx=300kΩ light_resistance_@100lx=400Ω luminance=10lx package=THT]
  J1 = Basic Servo

nets:
  GND: LED1.cathode, LED2.cathode, Bauteil1.GND, R5.pin_1, J1.gnd
  N1: LED1.anode, R1.Pin_1
  N2: LED2.anode, R2.Pin_1
  N3: R1.Pin_0, Bauteil1.D10_PWM/SS
  N4: R2.Pin_0, Bauteil1.D9_PWM
  N5: Bauteil1.A0, R4.Pin_1, R5.pin_0
  N6: Bauteil1.D6_PWM, J1.pulse
  5V: Bauteil1.5V, R4.Pin_0, J1.vcc

notes:
  FLIP FLOP

// code stored in the sketch: FlipFlop.ino
/*
  Flip Flop
  switching between two LEDs using a button
  
  This example is part of the Fritzing Creator Kit: www.fritzing.org/creator-kit.
*/

int buttonPin=2;                       // Pin where the button is attached
int greenLED=9;                        // Pin where the green LED is attached
int redLED=10;                         // Pin where the red LED is attached 

void setup(){
  pinMode(buttonPin, INPUT);           // button is initialised as INPUT 
  pinMode(greenLED, OUTPUT);           // green LED pin is initialised as OUTPUT 
  pinMode(redLED, OUTPUT);             // red LED pin is initialised as OUTPUT  
}

void loop(){
  if (digitalRead(buttonPin)==LOW){    // if the button is pressed (LOW) 
    digitalWrite(greenLED, HIGH);      // switch on green LED
    digitalWrite(redLED, LOW);         // switch off red LED
  } else {                             // else (if button is not pressed)
    digitalWrite(greenLED, LOW);       // switch off green LED
    digitalWrite(redLED, HIGH);        // switch on red LED
  }
}

// code stored in the sketch: Workshop_07_Servo.ino
#include <Servo.h>

Servo myservo;
int potpin = 0;
int val;

void setup()
{
  Serial.begin(9600);
  myservo.attach(6);
}

void loop() {
  val = analogRead(potpin);
  Serial.println(val);
  
  val = map(val, 0, 1023, 0, 179);
  
  myservo.write(val);
  
  delay(100);
}
