# Fritzing sketch Knock (saved by Fritzing 1.0.0d)
circuit board: 6.88566cm x 5.36311cm
breadboards: 2

parts:
  J2 = Piezo Speaker
  R5 = Resistor [resistance=1M tolerance=±5% power=0.25W package=THT]
  PCB1 = Arduino Shield PCB  # not connected
  Arduino1 = Arduino Uno (Rev3)

nets:
  N1: J2.pin1, R5.Pin_0, Arduino1.GND
  N2: J2.pin2, R5.Pin_1, Arduino1.A0

notes:
  A Piezo is an electronic device that can both be used to play tones and to detect tones. In this project, a Piezo captures a knock and sends a string "Knock!" back to the computer over the serial port. In order to see this text you can use the Arduino serial monitor.
  http://arduino.cc/en/Tutorial/Knock

custom parts:
  Arduino Shield PCB: Plain PCB Shaped to fit an Arduino "Shield"
