# Fritzing sketch LCD (saved by Fritzing 1.0.2b)
circuit board: 6.88566cm x 5.36311cm
breadboards: 2

parts:
  PCB1 = Arduino Shield PCB  # not connected
  LCD1 = LCD screen
  R2 = Resistor [tolerance=±5% resistance=220 power=0.25W package=THT]
  Arduino1 = Arduino Uno (Rev3)
  R3 = Rotary Potentiometer (Small) [maximum_resistance=10kΩ knob_status=50% power=0.5W package=THT]

nets:
  VSS: LCD1.VSS, LCD1.R/W, LCD1.LED-, Arduino1.GND, R3.leg1
  VDD: LCD1.VDD, R2.Pin_1, Arduino1.5V, R3.leg2
  N1: LCD1.V0, R3.wiper
  N2: LCD1.RS, Arduino1.D12/MISO
  N3: LCD1.E, Arduino1.D11_PWM/MOSI
  N4: LCD1.DB4, Arduino1.D5_PWM
  N5: LCD1.DB5, Arduino1.D4
  N6: LCD1.DB6, Arduino1.D3_PWM
  N7: LCD1.DB7, Arduino1.D2
  N8: LCD1.LED+, R2.Pin_0

notes:
  Code and more on character LCDs at http://arduino.cc/en/Tutorial/LiquidCrystal

custom parts:
  Arduino Shield PCB: Plain PCB Shaped to fit an Arduino "Shield"
