# Fritzing sketch LED-Matrix (saved by Fritzing 1.0.2b)
circuit board: 6.88566cm x 5.36311cm
breadboards: 2

parts:
  Q6 = PNP-Transistor [package="TO92 [THT]"]
  Q7 = PNP-Transistor [package="TO92 [THT]"]
  Q8 = PNP-Transistor [package="TO92 [THT]"]
  Q9 = PNP-Transistor [package="TO92 [THT]"]
  Q10 = PNP-Transistor [package="TO92 [THT]"]
  R6 = Resistor [tolerance=±5% resistance=1k power=0.25W package=THT]
  R7 = Resistor [tolerance=±5% resistance=1k power=0.25W package=THT]
  R8 = Resistor [tolerance=±5% resistance=1k power=0.25W package=THT]
  R9 = Resistor [tolerance=±5% resistance=1k power=0.25W package=THT]
  R10 = Resistor [tolerance=±5% resistance=1k power=0.25W package=THT]
  Dot_Matrix1 = LED Dot Matrix 18mm (0.7 INCH)
  Arduino1 = Arduino Uno (Rev3)

nets:
  N1: Q6.E, Q7.E, Q8.E, Q9.E, Q10.E, Arduino1.5V
  N2: Q6.B, R6.Pin_1
  N3: Q6.C, Dot_Matrix1.Column_1
  N4: Q7.B, R7.Pin_1
  N5: Q7.C, Dot_Matrix1.Column_2
  N6: Q8.B, R8.Pin_1
  N7: Q8.C, Dot_Matrix1.Column_4
  N8: Q9.B, R9.Pin_1
  N9: Q9.C, Dot_Matrix1.Column_5
  N10: Q10.B, R10.Pin_1
  N11: Q10.C, Dot_Matrix1.Column_3
  N12: R6.Pin_0, Arduino1.D1/TX
  N13: R7.Pin_0, Arduino1.D3_PWM
  N14: R8.Pin_0, Arduino1.D7
  N15: R9.Pin_0, Arduino1.D8
  N16: R10.Pin_0, Arduino1.D10_PWM/SS
  N17: Dot_Matrix1.Row_3, Arduino1.D2
  N18: Dot_Matrix1.Row_5, Arduino1.D4
  N19: Dot_Matrix1.Row_6, Arduino1.D5_PWM
  N20: Dot_Matrix1.Row_7, Arduino1.D6_PWM
  N21: Dot_Matrix1.Row_4, Arduino1.D9_PWM
  N22: Dot_Matrix1.Row_2, Arduino1.D11_PWM/MOSI
  N23: Dot_Matrix1.Row_1, Arduino1.D12/MISO

notes:
  Sketch by Johannes Findeisen
  www.hanez.org
  Find the Code here:
  Code
