# Fritzing sketch LED-Matrix_simple (saved by Fritzing 0.8.5b)
circuit board: 6.88566cm x 5.36311cm
breadboards: 2

parts:
  Arduino1 = Arduino Uno (Rev3)
  Dot_Matrix1 = LED Dot Matrix 18mm (0.7 INCH)

nets:
  N1: Arduino1.D8, Dot_Matrix1.Column_5
  N2: Arduino1.D9_PWM, Dot_Matrix1.Row_4
  N3: Arduino1.D10_PWM/SS, Dot_Matrix1.Column_3
  N4: Arduino1.D11_PWM/MOSI, Dot_Matrix1.Row_2
  N5: Arduino1.D12/MISO, Dot_Matrix1.Row_1
  N6: Arduino1.D1/TX, Dot_Matrix1.Column_1
  N7: Arduino1.D2, Dot_Matrix1.Row_3
  N8: Arduino1.D3_PWM, Dot_Matrix1.Column_2
  N9: Arduino1.D4, Dot_Matrix1.Row_5
  N10: Arduino1.D5_PWM, Dot_Matrix1.Row_6
  N11: Arduino1.D6_PWM, Dot_Matrix1.Row_7
  N12: Arduino1.D7, Dot_Matrix1.Column_4

notes:
  Sketch by Johannes Findeisen
  www.hanez.org
  Find the Code here:
  Code
