# Fritzing sketch Loop-SMD (saved by Fritzing 0.7.0b)
breadboards: 1

parts:
  R1 = Resistor [resistance=220 tolerance=±5% package="0805 [SMD]"]
  R2 = Resistor [resistance=220 tolerance=±5% package="0805 [SMD]"]
  R3 = Resistor [resistance=220 tolerance=±5% package="0805 [SMD]"]
  R4 = Resistor [resistance=220 tolerance=±5% package="0805 [SMD]"]
  R5 = Resistor [resistance=220 tolerance=±5% package="0805 [SMD]"]
  R6 = Resistor [resistance=220 tolerance=±5% package="0805 [SMD]"]
  LED1 = smd LED [color="Red (633nm)" package="0805 [SMD]"]
  LED2 = smd LED [color="Red (633nm)" package="0805 [SMD]"]
  LED4 = smd LED [color="Red (633nm)" package="0805 [SMD]"]
  LED5 = smd LED [color="Red (633nm)" package="0805 [SMD]"]
  LED3 = smd LED [color="Red (633nm)" package="0805 [SMD]"]
  LED6 = smd LED [color="Red (633nm)" package="0805 [SMD]"]
  Arduino = Arduino

nets:
  N1: R1.Pin_0, LED1.anode
  N2: R1.Pin_1, Arduino.D2
  N3: R2.Pin_0, LED2.anode
  N4: R2.Pin_1, Arduino.D3
  N5: R3.Pin_0, LED3.anode
  N6: R3.Pin_1, Arduino.D4
  N7: R4.Pin_0, LED4.anode
  N8: R4.Pin_1, Arduino.D5
  N9: R5.Pin_0, LED5.anode
  N10: R5.Pin_1, Arduino.D6
  N11: R6.Pin_0, LED6.anode
  N12: R6.Pin_1, Arduino.D7
  N13: LED1.cathode, LED2.cathode, LED4.cathode, LED5.cathode, LED3.cathode, LED6.cathode, Arduino.GND

notes:
  In this example, six leds are controlled by digital out pins. Related Example: http://arduino.cc/en/Tutorial/Loop

// code stored in the sketch: Loop_SMD.ino
/*
  For Loop Iteration
 
 Demonstrates the use of a for() loop. 
 Lights multiple LEDs in sequence, then in reverse.
 
 The circuit:
 * LEDs from pins 2 through 7 to ground
 
 created 2006
 by David A. Mellis
 modified 30 Aug 2011
 by Tom Igoe 

This example code is in the public domain.
 
 http://www.arduino.cc/en/Tutorial/ForLoop
 */

int timer = 100;           // The higher the number, the slower the timing.

void setup() {
  // use a for loop to initialize each pin as an output:
  for (int thisPin = 2; thisPin < 8; thisPin++)  {
    pinMode(thisPin, OUTPUT);      
  }
}

void loop() {
  // loop from the lowest pin to the highest:
  for (int thisPin = 2; thisPin < 8; thisPin++) { 
    // turn the pin on:
    digitalWrite(thisPin, HIGH);   
    delay(timer);                  
    // turn the pin off:
    digitalWrite(thisPin, LOW);    
  }

  // loop from the highest pin to the lowest:
  for (int thisPin = 7; thisPin >= 2; thisPin--) { 
    // turn the pin on:
    digitalWrite(thisPin, HIGH);
    delay(timer);
    // turn the pin off:
    digitalWrite(thisPin, LOW);
  }
}
