# Fritzing sketch Mood-Light (saved by Fritzing 1.0.0d)
circuit board: 6.88566cm x 5.36311cm
breadboards: 2

parts:
  R1 = Resistor [tolerance=±5% resistance=220 power=0.25W package=THT]
  R2 = Resistor [tolerance=±5% resistance=220 power=0.25W package=THT]
  R3 = Resistor [tolerance=±5% resistance=220 power=0.25W package=THT]
  LED1 = Super Flux RGB LED (com. anode)
  PCB1 = Arduino Shield PCB  # not connected
  Arduino1 = Arduino Uno (Rev3)

nets:
  N1: R1.Pin_0, Arduino1.D12/MISO
  N2: R1.Pin_1, LED1.red_cathode
  N3: R2.Pin_0, LED1.blue_cathode
  N4: R2.Pin_1, Arduino1.D11_PWM/MOSI
  N5: R3.Pin_0, LED1.green_cathode
  N6: R3.Pin_1, Arduino1.D10_PWM/SS
  N7: LED1.common_anode, Arduino1.5V

custom parts:
  Arduino Shield PCB: Plain PCB Shaped to fit an Arduino "Shield"
