# Fritzing sketch Optocoupler (saved by Fritzing 0.8.6b)
circuit board: 6.88566cm x 5.36311cm
breadboards: 2

parts:
  U1 = Optocoupler [package=THT]
  R3 = Resistor [resistance=220 tolerance=±5% package=THT]
  R4 = Resistor [resistance=220 tolerance=±5% package=THT]
  LED2 = LED - 5mm [color="Red (633nm)" package="5 mm [THT]"]
  VCC1 = Battery
  Arduino2 = Arduino Uno (Rev3)
  part = LED - 5mm [color="Red (633nm)" package="5 mm [THT]"]  # not connected

nets:
  N1: U1.Pin_1, R3.Pin_1
  N2: U1.Pin_2, Arduino2.GND
  N3: U1.Pin_4, VCC1.-
  N4: U1.Pin_5, LED2.cathode
  N5: R3.Pin_0, Arduino2.D11_PWM/MOSI
  N6: R4.Pin_0, LED2.anode
  N7: R4.Pin_1, VCC1.+

notes:
  An optocoupler can be used to control a circuit that's completely isolated from your microcontroller in order to avoid the risk of short-circuit. In this case, imagine that the LED + battery pack combo is a hacked toy that you're turning on and off with the Arduino.
