# Fritzing sketch Parking-Assistant (saved by Fritzing 1.0.2b)
circuit board: 6.88566cm x 5.36311cm
breadboards: 2

parts:
  LED7 = LED - 5mm [color="Red (633nm)" current=0.030A package="5 mm [THT]"]
  LED8 = LED - 5mm [color="Red (633nm)" current=0.030A package="5 mm [THT]"]
  LED9 = LED - 5mm [color="Red (633nm)" current=0.030A package="5 mm [THT]"]
  LED10 = LED - 5mm [color="Red (633nm)" current=0.030A package="5 mm [THT]"]
  LED11 = LED - 5mm [color="Yellow (585nm)" current=0.030A package="5 mm [THT]"]
  LED12 = LED - 5mm [color="Yellow (585nm)" current=0.030A package="5 mm [THT]"]
  LED13 = LED - 5mm [color="Yellow (585nm)" current=0.030A package="5 mm [THT]"]
  LED14 = LED - 5mm [color="Yellow (585nm)" current=0.030A package="5 mm [THT]"]
  LED15 = LED - 5mm [color="Yellow (585nm)" current=0.030A package="5 mm [THT]"]
  LED16 = LED - 5mm [color="Yellow (585nm)" current=0.030A package="5 mm [THT]"]
  220Ω1 = Resistor [resistance=220 tolerance=±5% power=0.25W package=THT]
  220Ω2 = Resistor [resistance=220 tolerance=±5% power=0.25W package=THT]
  220Ω3 = Resistor [resistance=220 tolerance=±5% power=0.25W package=THT]
  220Ω4 = Resistor [resistance=220 tolerance=±5% power=0.25W package=THT]
  220Ω5 = Resistor [resistance=220 tolerance=±5% power=0.25W package=THT]
  220Ω6 = Resistor [resistance=220 tolerance=±5% power=0.25W package=THT]
  220Ω7 = Resistor [resistance=220 tolerance=±5% power=0.25W package=THT]
  220Ω8 = Resistor [resistance=220 tolerance=±5% power=0.25W package=THT]
  220Ω9 = Resistor [resistance=220 tolerance=±5% power=0.25W package=THT]
  220Ω10 = Resistor [resistance=220 tolerance=±5% power=0.25W package=THT]
  Arduino1 = Arduino Uno (Rev3)
  J1 = Infrared Proximity Sensor [distance_to_obstacle=50%]
  J2 = Infrared Proximity Sensor [distance_to_obstacle=50%]

nets (from the schematic view):
  GND: LED7.cathode, LED8.cathode, LED9.cathode, LED10.cathode, LED11.cathode, LED12.cathode, LED13.cathode, LED14.cathode, LED15.cathode, LED16.cathode, Arduino1.GND, J1.GND, J2.GND
  N1: LED7.anode, 220Ω10.Pin_0
  N2: LED8.anode, 220Ω9.Pin_0
  N3: LED9.anode, 220Ω2.Pin_0
  N4: LED10.anode, 220Ω3.Pin_0
  N5: LED11.anode, 220Ω1.Pin_0
  N6: LED12.anode, 220Ω4.Pin_0
  N7: LED13.anode, 220Ω5.Pin_0
  N8: LED14.anode, 220Ω7.Pin_0
  N9: LED15.anode, 220Ω6.Pin_0
  N10: LED16.anode, 220Ω8.Pin_0
  N11: 220Ω1.Pin_1, Arduino1.D5_PWM
  N12: 220Ω2.Pin_1, Arduino1.D3_PWM
  N13: 220Ω3.Pin_1, Arduino1.D4
  N14: 220Ω4.Pin_1, Arduino1.D6_PWM
  N15: 220Ω5.Pin_1, Arduino1.D7
  N16: 220Ω6.Pin_1, Arduino1.D9_PWM
  N17: 220Ω7.Pin_1, Arduino1.D8
  N18: 220Ω8.Pin_1, Arduino1.D10_PWM/SS
  N19: 220Ω9.Pin_1, Arduino1.D11_PWM/MOSI
  N20: 220Ω10.Pin_1, Arduino1.D12/MISO
  N21: Arduino1.A0, J1.Vout
  N22: Arduino1.A1, J2.Vout
  VCC: Arduino1.5V, J1.Vcc, J2.Vcc

notes:
  Simple Parking Assistant
  The distance to objects in the proximity is measured and displayed as led graph.
