# Fritzing sketch RGB-LED (saved by Fritzing 1.0.0d)
circuit board: 6.88566cm x 5.36311cm
breadboards: 2

parts:
  R4 = Resistor [resistance=220 tolerance=±5% power=0.25W package=THT]
  R5 = Resistor [resistance=220 tolerance=±5% power=0.25W package=THT]
  R6 = Resistor [resistance=220 tolerance=±5% power=0.25W package=THT]
  PCB1 = Arduino Shield PCB  # not connected
  LED = RGB LED (com. cathode, rgb) [color="Red (633nm)" current=0.030A package="5 mm [THT]"]
  Arduino1 = Arduino Uno (Rev3)

nets:
  N1: R4.Pin_0, Arduino1.D11_PWM/MOSI
  N2: R4.Pin_1, LED.red_anode
  N3: R5.Pin_0, Arduino1.D9_PWM
  N4: R5.Pin_1, LED.blue_anode
  N5: R6.Pin_0, Arduino1.D10_PWM/SS
  N6: R6.Pin_1, LED.green_anode
  N7: LED.common_cathode, Arduino1.GND

notes:
  Let the light shine in any color!
  Check out this forum post for a good code example.

custom parts:
  Arduino Shield PCB: Plain PCB Shaped to fit an Arduino "Shield"
