# Fritzing sketch Relay (saved by Fritzing 1.0.0rc)
circuit board: 6.88566cm x 5.36311cm
breadboards: 2

parts:
  Power_plug2 = Power plug
  M2 = DC Motor [voltage_(max)=6V voltage_(min)=3V]
  D3 = Rectifier Diode [part_number=1N4001 package="300 mil [THT]"]
  R4 = Resistor [resistance=1k tolerance=±5% power=0.25W package=THT]
  Q3 = NPN-Transistor [package="TO92 [THT]"]
  PCB1 = Arduino Shield PCB  # not connected
  Arduino1 = Arduino Uno (Rev3)
  K3 = Relay [part_number=FRS1B-S package=THT]

nets:
  N1: Power_plug2.GND, M2.pin_2
  N2: Power_plug2.VCC, K3.C1, K3.C2
  N3: M2.pin_1, K3.A
  N4: D3.cathode, Arduino1.5V, K3.COIL2
  N5: D3.anode, Q3.C, K3.COIL1
  N6: R4.Pin_0, Q3.B
  N7: R4.Pin_1, Arduino1.D3_PWM
  N8: Q3.E, Arduino1.GND

notes:
  In this circuit a 5V relay is connected to the arduino board and controls a DC motor which is connected to an external power supply.

custom parts:
  Arduino Shield PCB: Plain PCB Shaped to fit an Arduino "Shield"
