# Fritzing sketch Sabotage-Detection (saved by Fritzing 1.0.2b)
circuit board: 6.88566cm x 5.36311cm
breadboards: 2

parts:
  S2 = Pushbutton [package="[THT]"]
  R6 = Resistor [tolerance=±5% resistance=220 power=0.25W package=THT]
  R7 = Resistor [tolerance=±5% resistance=1.1k power=0.25W package=THT]
  R8 = Resistor [tolerance=±5% resistance=220 power=0.25W package=THT]
  R9 = Resistor [tolerance=±5% resistance=220 power=0.25W package=THT]
  LED6 = LED - 5mm [color="Green (555nm)" current=0.030A package="5 mm [THT]"]
  ADXL335 = Triple Axis Accelerometer Breakout - ADXL335
  LED7 = Super Flux LED blue [color=Red current=0.030A]
  PCB1 = Arduino Shield PCB  # not connected
  Arduino1 = Arduino Uno (Rev3)
  LED8 = Super Flux LED blue [color=Blue current=0.030A]
  R11 = Rotary Potentiometer (Small) [maximum_resistance=10kΩ knob_status=50% power=0.5W package=THT]

nets:
  N1: S2.Pin_1, S2.Pin_2, Arduino1.5V, R11.leg1
  N2: S2.Pin_3, S2.Pin_4, R7.Pin_1, Arduino1.D2
  GND: R6.Pin_0, R7.Pin_0, R8.Pin_0, R9.Pin_0, ADXL335.GND, Arduino1.GND, R11.leg2
  N3: R6.Pin_1, LED6.cathode
  N4: R8.Pin_1, LED7.cathode
  N5: R9.Pin_1, LED8.cathode
  N6: LED6.anode, Arduino1.D11_PWM/MOSI
  N7: ADXL335.ZOUT, Arduino1.A0
  N8: ADXL335.YOUT, Arduino1.A1
  N9: ADXL335.XOUT, Arduino1.A2
  VCC: ADXL335.VCC, Arduino1.3V3
  N10: LED7.anode, Arduino1.D3_PWM
  N11: Arduino1.A3, R11.wiper
  N12: Arduino1.D7, LED8.anode

notes:
  Get the Arduino Code from here:
  Sabotage Alert

custom parts:
  Arduino Shield PCB: Plain PCB Shaped to fit an Arduino "Shield"

// code stored in the sketch: Sabotage-Detection.ino
/*
  _____       .__  __         .__                
_/ ____\______|__|/  |________|__| ____    ____  
\   __\\_  __ \  \   __\___   /  |/    \  / ___\ 
 |  |   |  | \/  ||  |  /    /|  |   |  \/ /_/  >
 |__|   |__|  |__||__| /_____ \__|___|  /\___  / 
                             \/       \//_____/  
  
Example      Sabotage Detection
Autor        Stefan Hermann
Date         5.12.2011

*/

int myState=0;
int greenLedPin=11;
int redLedPin=7;
int blueLedPin=3;
int buttonPin=2;
int potPin=3;
int accZPin=0;
int accYPin=1;
int accXPin=2;

int startAccZ;
int startAccY;
int startAccX;

void setup(){
  pinMode(greenLedPin,OUTPUT);
  pinMode(redLedPin,OUTPUT);
  pinMode(blueLedPin,OUTPUT);
  pinMode(buttonPin,INPUT);
  startAccZ=analogRead(accZPin);
  startAccY=analogRead(accYPin);
  startAccX=analogRead(accXPin);
}

void alertBlinking(){
  digitalWrite(redLedPin,HIGH);
  delay(50);
  digitalWrite(redLedPin,LOW);
  delay(100);
  digitalWrite(blueLedPin,HIGH);
  delay(50);
  digitalWrite(blueLedPin,LOW); 
  delay(100);  
}

boolean senseAcceleration(int myPotVal){
  boolean myReturn=false;
  myPotVal=map(myPotVal,0,1023,0,10);
  if (analogRead(accXPin)>startAccX+myPotVal) myReturn=true;
  if (analogRead(accYPin)>startAccY+myPotVal) myReturn=true;
  if (analogRead(accZPin)>startAccZ+myPotVal) myReturn=true;
  return myReturn;
}

void loop(){
  //alertBlinking();
  switch (myState){
  case 0: //idle
    if (senseAcceleration(analogRead(potPin))==true) {
      digitalWrite(greenLedPin,LOW);
      myState=1;
    } else {
      digitalWrite(greenLedPin,HIGH);    
    };
    break;
  case 1: // alert
    alertBlinking();
    if (digitalRead(buttonPin)==HIGH){
      myState=0;
    }
    break;
  }
  delay(10);
}
