# Fritzing sketch Shift_Register (saved by Fritzing 0.7.0b)
breadboards: 2

parts:
  74HC5951 = 74HC595 [package="DIP16 [THT]"]
  R2 = Resistor [resistance=220 tolerance=±5% package=THT]
  R3 = Resistor [resistance=220 tolerance=±5% package=THT]
  R4 = Resistor [resistance=220 tolerance=±5% package=THT]
  R5 = Resistor [resistance=220 tolerance=±5% package=THT]
  R6 = Resistor [resistance=220 tolerance=±5% package=THT]
  R7 = Resistor [resistance=220 tolerance=±5% package=THT]
  R8 = Resistor [resistance=220 tolerance=±5% package=THT]
  R9 = Resistor [resistance=220 tolerance=±5% package=THT]
  C2 = Ceramic Capacitor [capacitance=100nF rated_voltage=35V package="200 mil [THT, multilayer]"]
  LED6 = LED - 5mm [color="Red (633nm)" package="5 mm [THT]"]
  LED5 = LED - 5mm [color="Red (633nm)" package="5 mm [THT]"]
  LED4 = LED - 5mm [color="Red (633nm)" package="5 mm [THT]"]
  LED9 = LED - 5mm [color="Red (633nm)" package="5 mm [THT]"]
  LED3 = LED - 5mm [color="Red (633nm)" package="5 mm [THT]"]
  LED8 = LED - 5mm [color="Red (633nm)" package="5 mm [THT]"]
  LED2 = LED - 5mm [color="Red (633nm)" package="5 mm [THT]"]
  LED7 = LED - 5mm [color="Red (633nm)" package="5 mm [THT]"]
  Arduino1 = Arduino

nets:
  N1: 74HC5951.Q1, R5.Pin_1
  N2: 74HC5951.Q2, R6.Pin_1
  N3: 74HC5951.Q3, R7.Pin_1
  N4: 74HC5951.Q4, R9.Pin_1
  N5: 74HC5951.Q5, R2.Pin_1
  N6: 74HC5951.Q6, R3.Pin_1
  N7: 74HC5951.Q7, R8.Pin_1
  GND: 74HC5951.GND, 74HC5951.OE, C2.1, LED6.cathode, LED5.cathode, LED4.cathode, LED9.cathode, LED3.cathode, LED8.cathode, LED2.cathode, LED7.cathode, Arduino1.GND
  5V: 74HC5951.MR, 74HC5951.VCC, Arduino1.+5V
  N8: 74HC5951.SH_CP, Arduino1.D12
  N9: 74HC5951.ST_CP, C2.0, Arduino1.D8
  N10: 74HC5951.DS, Arduino1.D11
  N11: 74HC5951.Q0, R4.Pin_1
  N12: R2.Pin_0, LED6.anode
  N13: R3.Pin_0, LED8.anode
  N14: R4.Pin_0, LED9.anode
  N15: R5.Pin_0, LED4.anode
  N16: R6.Pin_0, LED2.anode
  N17: R7.Pin_0, LED5.anode
  N18: R8.Pin_0, LED7.anode
  N19: R9.Pin_0, LED3.anode

notes:
  In this project, a 74HC595 shift register is used to control 8 LEDs with just 3 Arduino pins.
  Related example: http://www.arduino.cc/en/Tutorial/ShiftOut

// code stored in the sketch: Shift_Register.ino
/*
  Shift Register Example
 for 74HC595 shift register

 This sketch turns reads serial input and uses it to set the pins
 of a 74HC595 shift register.

 Hardware:
 * 74HC595 shift register attached to pins 2, 3, and 4 of the Arduino,
 as detailed below.
 * LEDs attached to each of the outputs of the shift register

 Created 22 May 2009
 Created 23 Mar 2010
 by Tom Igoe

 */

//Pin connected to latch pin (ST_CP) of 74HC595
const int latchPin = 8;
//Pin connected to clock pin (SH_CP) of 74HC595
const int clockPin = 12;
////Pin connected to Data in (DS) of 74HC595
const int dataPin = 11;

void setup() {
  //set pins to output because they are addressed in the main loop
  pinMode(latchPin, OUTPUT);
  pinMode(dataPin, OUTPUT);  
  pinMode(clockPin, OUTPUT);
  Serial.begin(9600);
  Serial.println("reset");
}

void loop() {
  if (Serial.available() > 0) {
    // ASCII '0' through '9' characters are
    // represented by the values 48 through 57.
    // so if the user types a number from 0 through 9 in ASCII, 
    // you can subtract 48 to get the actual value:
    int bitToSet = Serial.read() - 48;

  // write to the shift register with the correct bit set high:
    registerWrite(bitToSet, HIGH);
  }
}

// This method sends bits to the shift register:

void registerWrite(int whichPin, int whichState) {
// the bits you want to send
  byte bitsToSend = 0;

  // turn off the output so the pins don't light up
  // while you're shifting bits:
  digitalWrite(latchPin, LOW);

  // turn on the next highest bit in bitsToSend:
  bitWrite(bitsToSend, whichPin, whichState);

  // shift the bits out:
  shiftOut(dataPin, clockPin, MSBFIRST, bitsToSend);

    // turn on the output so the LEDs can light up:
  digitalWrite(latchPin, HIGH);

}
