# Fritzing sketch Shift_Register_2x (saved by Fritzing 1.0.2b)
circuit board: 6.88176cm x 9.61717cm
breadboards: 2

parts:
  R10 = Resistor [resistance=220 tolerance=±5% power=0.25W package=THT]
  R11 = Resistor [resistance=220 tolerance=±5% power=0.25W package=THT]
  R12 = Resistor [resistance=220 tolerance=±5% power=0.25W package=THT]
  R13 = Resistor [resistance=220 tolerance=±5% power=0.25W package=THT]
  R14 = Resistor [resistance=220 tolerance=±5% power=0.25W package=THT]
  R15 = Resistor [resistance=220 tolerance=±5% power=0.25W package=THT]
  R16 = Resistor [resistance=220 tolerance=±5% power=0.25W package=THT]
  R17 = Resistor [resistance=220 tolerance=±5% power=0.25W package=THT]
  LED10 = LED - 5mm [color="Red (633nm)" current=0.030A package="5 mm [THT]"]
  LED11 = LED - 5mm [color="Red (633nm)" current=0.030A package="5 mm [THT]"]
  LED12 = LED - 5mm [color="Red (633nm)" current=0.030A package="5 mm [THT]"]
  LED13 = LED - 5mm [color="Red (633nm)" current=0.030A package="5 mm [THT]"]
  LED14 = LED - 5mm [color="Red (633nm)" current=0.030A package="5 mm [THT]"]
  LED15 = LED - 5mm [color="Red (633nm)" current=0.030A package="5 mm [THT]"]
  LED16 = LED - 5mm [color="Red (633nm)" current=0.030A package="5 mm [THT]"]
  LED17 = LED - 5mm [color="Red (633nm)" current=0.030A package="5 mm [THT]"]
  74HC5952 = 74HC595 [package="DIP16 [THT]"]
  C3 = Ceramic Capacitor [capacitance=100nF rated_voltage=35V package="200 mil [THT, multilayer]"]
  LED18 = LED - 5mm [color="Red (633nm)" current=0.030A package="5 mm [THT]"]
  LED19 = LED - 5mm [color="Red (633nm)" current=0.030A package="5 mm [THT]"]
  LED20 = LED - 5mm [color="Red (633nm)" current=0.030A package="5 mm [THT]"]
  LED21 = LED - 5mm [color="Red (633nm)" current=0.030A package="5 mm [THT]"]
  LED22 = LED - 5mm [color="Red (633nm)" current=0.030A package="5 mm [THT]"]
  LED23 = LED - 5mm [color="Red (633nm)" current=0.030A package="5 mm [THT]"]
  LED24 = LED - 5mm [color="Red (633nm)" current=0.030A package="5 mm [THT]"]
  LED25 = LED - 5mm [color="Red (633nm)" current=0.030A package="5 mm [THT]"]
  R18 = Resistor [resistance=220 tolerance=±5% power=0.25W package=THT]
  R19 = Resistor [resistance=220 tolerance=±5% power=0.25W package=THT]
  R20 = Resistor [resistance=220 tolerance=±5% power=0.25W package=THT]
  R21 = Resistor [resistance=220 tolerance=±5% power=0.25W package=THT]
  R22 = Resistor [resistance=220 tolerance=±5% power=0.25W package=THT]
  R23 = Resistor [resistance=220 tolerance=±5% power=0.25W package=THT]
  R24 = Resistor [resistance=220 tolerance=±5% power=0.25W package=THT]
  R25 = Resistor [resistance=220 tolerance=±5% power=0.25W package=THT]
  74HC5953 = 74HC595 [package="DIP16 [THT]"]
  Arduino1 = Arduino Uno (Rev3)

nets:
  N1: R10.Pin_0, LED14.anode
  N2: R10.Pin_1, 74HC5952.Q6
  N3: R11.Pin_0, LED10.anode
  N4: R11.Pin_1, 74HC5952.Q5
  N5: R12.Pin_0, LED12.anode
  N6: R12.Pin_1, 74HC5952.Q4
  N7: R13.Pin_0, LED11.anode
  N8: R13.Pin_1, 74HC5952.Q7
  N9: R14.Pin_0, LED13.anode
  N10: R14.Pin_1, 74HC5952.Q3
  N11: R15.Pin_0, LED15.anode
  N12: R15.Pin_1, 74HC5952.Q2
  N13: R16.Pin_0, LED16.anode
  N14: R16.Pin_1, 74HC5952.Q1
  N15: R17.Pin_0, LED17.anode
  N16: R17.Pin_1, 74HC5952.Q0
  GND: LED10.cathode, LED11.cathode, LED12.cathode, LED13.cathode, LED14.cathode, LED15.cathode, LED16.cathode, LED17.cathode, 74HC5952.GND, 74HC5952.OE, C3.1, LED18.cathode, LED19.cathode, LED20.cathode, LED21.cathode, LED22.cathode, LED23.cathode, LED24.cathode, LED25.cathode, 74HC5953.GND, 74HC5953.OE, Arduino1.GND
  VCC: 74HC5952.MR, 74HC5952.VCC, 74HC5953.MR, 74HC5953.VCC, Arduino1.5V
  N17: 74HC5952.SH_CP, 74HC5953.SH_CP, Arduino1.D12/MISO
  N18: 74HC5952.ST_CP, C3.0, 74HC5953.ST_CP, Arduino1.D8
  N19: 74HC5952.DS, 74HC5953.Q7', Arduino1.D11_PWM/MOSI
  N20: LED18.anode, R19.Pin_0
  N21: LED19.anode, R21.Pin_0
  N22: LED20.anode, R20.Pin_0
  N23: LED21.anode, R22.Pin_0
  N24: LED22.anode, R18.Pin_0
  N25: LED23.anode, R23.Pin_0
  N26: LED24.anode, R24.Pin_0
  N27: LED25.anode, R25.Pin_0
  N28: R18.Pin_1, 74HC5953.Q6
  N29: R19.Pin_1, 74HC5953.Q5
  N30: R20.Pin_1, 74HC5953.Q4
  N31: R21.Pin_1, 74HC5953.Q7
  N32: R22.Pin_1, 74HC5953.Q3
  N33: R23.Pin_1, 74HC5953.Q2
  N34: R24.Pin_1, 74HC5953.Q1
  N35: R25.Pin_1, 74HC5953.Q0

notes:
  In this project, two 74HC595 shift register are used to control 16 LEDs with just 3 Arduino pins.
  Related example: http://www.arduino.cc/en/Tutorial/ShiftOut

// code stored in the sketch: Shift_Register_2x.ino
//**************************************************************//
//  Name    : shiftOutCode, Dual One By One                           //
//  Author  : Carlyn Maw, Tom Igoe                               //
//  Date    : 25 Oct, 2006                                       //
//  Version : 1.0                                                //
//  Notes   : Code for using a 74HC595 Shift Register            //
//          : to count from 0 to 255                             //
//**************************************************************//

//Pin connected to ST_CP of 74HC595
int latchPin = 8;
//Pin connected to SH_CP of 74HC595
int clockPin = 12;
////Pin connected to DS of 74HC595
int dataPin = 11;

//holder for infromation you're going to pass to shifting function
byte data = 0; 



void setup() {
  //set pins to output because they are addressed in the main loop
  pinMode(latchPin, OUTPUT);

}

void loop() {

  //function that blinks all the LEDs
  //gets passed the number of blinks and the pause time
  blinkAll_2Bytes(1,500); 

  // light each pin one by one using a function A
  for (int j = 0; j < 8; j++) {
    //ground latchPin and hold low for as long as you are transmitting
    digitalWrite(latchPin, 0);
    //red LEDs
    lightShiftPinA(7-j);
    //green LEDs
    lightShiftPinA(j);
    //return the latch pin high to signal chip that it 
    //no longer needs to listen for information
    digitalWrite(latchPin, 1);
    delay(1000);
  }

  // light each pin one by one using a function A
  for (int j = 0; j < 8; j++) {
    //ground latchPin and hold low for as long as you are transmitting
    digitalWrite(latchPin, 0);
    //red LEDs
    lightShiftPinB(j);
    //green LEDs
    lightShiftPinB(7-j);
    //return the latch pin high to signal chip that it 
    //no longer needs to listen for information
    digitalWrite(latchPin, 1);
    delay(1000);
  } 

}

//This function uses bitwise math to move the pins up
void lightShiftPinA(int p) {
  //defines a local variable
  int pin;

  //this is line uses a bitwise operator
  //shifting a bit left using << is the same
  //as multiplying the decimal number by two. 
  pin = 1<< p;

  //move 'em out
  shiftOut(dataPin, clockPin, pin);   

}

//This function uses that fact that each bit in a byte
//is 2 times greater than the one before it to
//shift the bits higher
void lightShiftPinB(int p) {
  //defines a local variable
  int pin;

  //start with the pin = 1 so that if 0 is passed to this
  //function pin 0 will light. 
  pin = 1;

  for (int x = 0; x < p; x++) {
    pin = pin * 2; 
  }
  //move 'em out
  shiftOut(dataPin, clockPin, pin);   
}


// the heart of the program
void shiftOut(int myDataPin, int myClockPin, byte myDataOut) {
  // This shifts 8 bits out MSB first, 
  //on the rising edge of the clock,
  //clock idles low

  //internal function setup
  int i=0;
  int pinState;
  pinMode(myClockPin, OUTPUT);
  pinMode(myDataPin, OUTPUT);

  //clear everything out just in case to
  //prepare shift register for bit shifting
  digitalWrite(myDataPin, 0);
  digitalWrite(myClockPin, 0);

  //for each bit in the byte myDataOut?
  //NOTICE THAT WE ARE COUNTING DOWN in our for loop
  //This means that %00000001 or "1" will go through such
  //that it will be pin Q0 that lights. 
  for (i=7; i>=0; i--)  {
    digitalWrite(myClockPin, 0);

    //if the value passed to myDataOut and a bitmask result 
    // true then... so if we are at i=6 and our value is
    // %11010100 it would the code compares it to %01000000 
    // and proceeds to set pinState to 1.
    if ( myDataOut & (1<<i) ) {
      pinState= 1;
    }
    else {	
      pinState= 0;
    }

    //Sets the pin to HIGH or LOW depending on pinState
    digitalWrite(myDataPin, pinState);
    //register shifts bits on upstroke of clock pin  
    digitalWrite(myClockPin, 1);
    //zero the data pin after shift to prevent bleed through
    digitalWrite(myDataPin, 0);
  }

  //stop shifting
  digitalWrite(myClockPin, 0);
}


//blinks both registers based on the number of times you want to 
//blink "n" and the pause between them "d"
//starts with a moment of darkness to make sure the first blink
//has its full visual effect.
void blinkAll_2Bytes(int n, int d) {
  digitalWrite(latchPin, 0);
  shiftOut(dataPin, clockPin, 0);
  shiftOut(dataPin, clockPin, 0);
  digitalWrite(latchPin, 1);
  delay(200);
  for (int x = 0; x < n; x++) {
    digitalWrite(latchPin, 0);
    shiftOut(dataPin, clockPin, 255);
    shiftOut(dataPin, clockPin, 255);
    digitalWrite(latchPin, 1);
    delay(d);
    digitalWrite(latchPin, 0);
    shiftOut(dataPin, clockPin, 0);
    shiftOut(dataPin, clockPin, 0);
    digitalWrite(latchPin, 1);
    delay(d);
  }
}
