# Fritzing sketch measure_resistance (saved by Fritzing 1.0.2b)
circuit board: 3.66476cm x 1.13117cm
breadboards: 1

parts:
  R1 = Resistor [tolerance=±5% power=0.25 resistance=220 package=THT]
  R2 = Resistor [tolerance=±5% power=0.25 resistance=220 package=THT]
  VM1 = Multimeter (Ohmmeter)

nets:
  N1: R1.Pin_0, VM1.COM_Probe
  N2: R1.Pin_1, R2.Pin_0
  N3: R2.Pin_1, VM1.V_Probe

notes:
  Press the "Start Simulation" button to start the simulator. It will simulate your circuit when you change your circuit. To stop the simulator, press the "Stop Simulator" button.
  If you do not see the "Start Simulator" button, go to Edit->Preferences and enable the simulator in the "Beta Features" tab.
  This multimeter will measure the resistance of two resistor in series.
  Add more resistor or set them in parallel and see how the resistance changes!
