# Fritzing sketch nand_gate (saved by Fritzing 0.9.10b)
circuit board: 12.0449cm x 5.68872cm
breadboards: 1

parts:
  VM1 = Multimeter (DC Voltage)
  VCC1 = 4 x AAA Battery Mount
  R2 = Resistor [tolerance=±5% power=0.25 resistance=100 package=THT]
  R3 = Resistor [tolerance=±5% power=0.25 resistance=100 package=THT]
  LED1 = LED - 5mm [color="Red (633nm)" current=0.030 package="5 mm [THT]"]
  R4 = Resistor [tolerance=±5% power=0.25 resistance=100 package=THT]
  LED2 = LED - 5mm [color="Red (633nm)" current=0.030 package="5 mm [THT]"]
  LED3 = LED - 5mm [color="Red (633nm)" current=0.030 package="5 mm [THT]"]
  S1 = Pushbutton [package=THT]
  U1 = 4011 4 x 2 Input NAND Gate, single part [part_number=4011 package="DIP (Dual Inline) [THT]"]
  S2 = Pushbutton [package=THT]

nets:
  GND: VM1.COM_Probe, VCC1.-, R2.Pin_1, R3.Pin_1, R4.Pin_1, U1.GND
  OUT: VM1.V_Probe, LED1.anode, U1.Q1
  5V: VCC1.+, S1.leg0, U1.VDD, S2.leg0
  N1: R2.Pin_0, LED2.cathode
  N2: R3.Pin_0, LED3.cathode
  N3: LED1.cathode, R4.Pin_0
  IN1: LED2.anode, S1.leg1, U1.A1
  IN2: LED3.anode, U1.B1, S2.leg1

notes:
  Input signals
  NAND gate
  Power
  Voltmeter
  Output LED
  Input LEDs
  IN1
  IN2
  NAND GATE
  OUT
