# Fritzing sketch simple_potentiometer (saved by Fritzing 0.9.8b)
breadboards: 1

parts:
  VCC1 = Battery
  R2 = Rotary Potentiometer (Small) [maximum_resistance=100kΩ package=THT]
  VM1 = Multimeter (DC Voltage)

nets:
  GND: VCC1.-, R2.leg1, VM1.COM_Probe
  N1: VCC1.+, R2.leg2
  N2: R2.wiper, VM1.V_Probe

notes:
  Press the "Start Simulation" button to start the simulator. It will simulate your circuit when you change your circuit. To stop the simulator, press the "Stop Simulator" button.
  If you do not see the "Start Simulator" button, go to Edit->Preferences and enable the simulator in the "Beta Features" tab.
  Observe how the voltage changes when you move the knob of the potentiometer (change "knob status" in the Inspector pane).
