# Fritzing sketch flipflop_led_flashing_circuit (saved by Fritzing 1.0.3b)
breadboards: 1

parts:
  Q1 = NPN-Transistor [package="TO92 [THT]"]
  C1 = Electrolytic Capacitor [capacitance=0.1mF voltage=20V package="100 mil [THT, electrolytic]"]
  R1 = Resistor [tolerance=±5% power=0.25W resistance=470 package=THT]
  LED1 = LED - 5mm [color="Red (633nm)" current=0.030A package="5 mm [THT]"]
  R3 = Resistor [tolerance=±5% power=0.25W resistance=10k package=THT]
  Q2 = NPN-Transistor [package="TO92 [THT]"]
  C2 = Electrolytic Capacitor [capacitance=0.1mF voltage=20V package="100 mil [THT, electrolytic]"]
  LED2 = LED - 5mm [color="Red (633nm)" current=0.030A package="5 mm [THT]"]
  Oscilloscope1 = Oscilloscope [volts/div=1V time/div=1s ch1_offset=0V ch2_offset=5V ch3_offset=0V ch4_offset=0V ch1_volts/div=5V ch2_volts/div=5V ch3_volts/div=5V ch4_volts/div=5V horizontal_position=0s]
  VCC1 = Battery block 9V [internal_resistance=0.1Ω]
  R4 = Resistor [tolerance=±5% power=0.25W resistance=470 package=THT]
  R2 = Resistor [tolerance=±5% power=0.25W resistance=10k package=THT]
  P1 = Multimeter straight red probe
  P2 = Multimeter straight red probe

nets:
  GND: Q1.E, Q2.E, Oscilloscope1.COM_Probe, VCC1.-
  N1: Q1.B, C2.-, R2.Pin_1
  left: Q1.C, C1.+, LED1.cathode, Oscilloscope1.V2_Probe, P1.Probe_tip, P1.Probe_meter_end
  N2: C1.-, R3.Pin_1, Q2.B
  N3: R1.Pin_0, R3.Pin_0, VCC1.+, R4.Pin_0, R2.Pin_0
  N4: R1.Pin_1, LED1.anode
  right: Q2.C, C2.+, LED2.cathode, Oscilloscope1.V3_Probe, P2.Probe_tip, P2.Probe_meter_end
  N5: LED2.anode, R4.Pin_1
