# Fritzing sketch full_wave_rectifier (saved by Fritzing 1.0.0rc)
breadboards: 1

parts:
  U1 = Transformer [Lin=9 Lout=100 Rin=1Ω Rout=1Ω package=transformer]
  Oscilloscope1 = Oscilloscope [volts/div=1V time/div=10µs ch1_offset=0V ch2_offset=0V ch3_offset=0V ch4_offset=5V ch1_volts/div=5V ch2_volts/div=5V ch3_volts/div=5V ch4_volts/div=10V horizontal_position=0s]
  V1 = AC Power [voltage=5V amplitude=5V frequency=60Hz offset_voltage=0V delay_time=0s damping_factor=0s-1 phase=0degrees]
  Oscilloscope2 = Oscilloscope [volts/div=1V time/div=10ms ch1_offset=0V ch2_offset=0V ch3_offset=0V ch4_offset=0V ch1_volts/div=5V ch2_volts/div=5V ch3_volts/div=5V ch4_volts/div=5V horizontal_position=0s]
  C1 = Ceramic Capacitor [capacitance=99µF voltage=35V package="100 mil [THT, multilayer]"]

nets:
  N1: U1.1, Oscilloscope1.V2_Probe, V1.V+, Oscilloscope2.V1_Probe
  GND: U1.2, U1.4, Oscilloscope1.V1_Probe, V1.V-, Oscilloscope2.COM_Probe
  N2: U1.3, Oscilloscope1.COM_Probe, C1.1
