# Fritzing sketch TrafficLight (saved by Fritzing 1.0.2b)
circuit board: 6.88566cm x 5.36311cm
breadboards: 2

parts:
  LED1 = LED - 5mm [color="Red (633nm)" current=0.030A package="5 mm [THT]"]
  LED2 = LED - 5mm [color="Yellow (592nm)" current=0.030A package="5 mm [THT]"]
  LED3 = LED - 5mm [color="Green (555nm)" current=0.030A package="5 mm [THT]"]
  LED4 = LED - 5mm [color="Red (633nm)" current=0.030A package="5 mm [THT]"]
  LED5 = LED - 5mm [color="Green (555nm)" current=0.030A package="5 mm [THT]"]
  R1 = Resistor [tolerance=±5% resistance=220 power=0.25W package=THT]
  R2 = Resistor [tolerance=±5% resistance=220 power=0.25W package=THT]
  R3 = Resistor [tolerance=±5% resistance=220 power=0.25W package=THT]
  R4 = Resistor [tolerance=±5% resistance=220 power=0.25W package=THT]
  R5 = Resistor [tolerance=±5% resistance=220 power=0.25W package=THT]
  S1 = Pushbutton [package=THT]
  R6 = Resistor [tolerance=±5% resistance=100k power=0.25W package=THT]
  Arduino1 = Arduino Uno (Rev3)

nets:
  N1: LED1.cathode, R1.Pin_0
  N2: LED1.anode, Arduino1.D12/MISO
  N3: LED2.cathode, R2.Pin_0
  N4: LED2.anode, Arduino1.D11_PWM/MOSI
  N5: LED3.cathode, R3.Pin_0
  N6: LED3.anode, Arduino1.D10_PWM/SS
  N7: LED4.cathode, R4.Pin_0
  N8: LED4.anode, Arduino1.D9_PWM
  N9: LED5.cathode, R5.Pin_0
  N10: LED5.anode, Arduino1.D8
  N11: R1.Pin_1, R2.Pin_1, R3.Pin_1, R4.Pin_1, R5.Pin_1, R6.Pin_1, Arduino1.GND
  N12: S1.leg0, R6.Pin_0, Arduino1.D2
  N13: S1.leg1, Arduino1.5V

notes:
  Pedestrian Traffic Light
  Car Traffic Light
  This circuit can be coded such that both the car and pedestrian traffic lights go through their normal cycle until the button is pressed by a pedestrian. In this case, the lights will change in favor of the pedestrian.
