# Fritzing sketch VirtualColorMixer (saved by Fritzing 1.0.2b)
circuit board: 6.88566cm x 5.36311cm
breadboards: 2

parts:
  PCB1 = Arduino Shield PCB  # not connected
  Arduino1 = Arduino Uno (Rev3)
  R3 = Rotary Potentiometer (Small) [maximum_resistance=10kΩ knob_status=50% power=0.5W package=THT]
  R2 = Rotary Potentiometer (Small) [maximum_resistance=10kΩ knob_status=50% power=0.5W package=THT]
  R1 = Rotary Potentiometer (Small) [maximum_resistance=10kΩ knob_status=50% power=0.5W package=THT]

nets:
  N1: Arduino1.A0, R1.wiper
  N2: Arduino1.A1, R2.wiper
  N3: Arduino1.A2, R3.wiper
  N4: Arduino1.GND, R3.leg1, R2.leg1, R1.leg1
  N5: Arduino1.5V, R3.leg2, R2.leg2, R1.leg2

notes:
  You can send multiple values from the Arduino board to the computer using the serial print function. In this project, the analog values from three potentiometers are used to set the red, green, and blue values of the background color of a Processing sketch running on the computer.
  http://arduino.cc/en/Tutorial/VirtualColorMixer

custom parts:
  Arduino Shield PCB: Plain PCB Shaped to fit an Arduino "Shield"
