# Fritzing sketch VoltageRegulator_with_switch (saved by Fritzing 0.8.6b)
circuit board: 3.29672cm x 1.87694cm
breadboards: 2

parts:
  U2 = Voltage Regulator - 5V [package="TO220 [THT]"]
  C3 = Electrolytic Capacitor [capacitance=100nF rated_voltage=35V package="100 mil [THT, electrolytic]"]
  C4 = Electrolytic Capacitor [capacitance=100nF rated_voltage=35V package="100 mil [THT, electrolytic]"]
  J4 = female pin header, 2 pins [form="♂ (male)"]
  S3 = Toggle Switch [package=THT]
  Power_plug2 = Power plug
  part = Power plug  # not connected

nets:
  N1: U2.input_voltage, C4.+, S3.L2
  GND: U2.GND, C3.-, C4.-, J4.pin2, Power_plug2.GND
  N2: U2.output_voltage, C3.+, J4.pin1
  N3: S3.COM, Power_plug2.VCC

notes:
  This example uses a 7805 voltage regulator to regulate voltage to 5 volts. There is a switch to turn power to the circuit on and off. The battery should be at least 7V DC.
  +
  -
