# Fritzing sketch Window_Alarm (saved by Fritzing 0.8.6b)
circuit board: 6.88566cm x 5.36311cm
breadboards: 2

parts:
  Speaker1 = Piezo Speaker
  R3 = Resistor [resistance=10k tolerance=±5% package=THT]
  Reed_Switch1 = Reed switch [package=THT]
  Arduino1 = Arduino Uno (Rev3)
  part = Reed switch [package=THT]  # not connected

nets:
  N1: Speaker1.pin1, R3.Pin_1, Arduino1.GND
  N2: Speaker1.pin2, Arduino1.D9_PWM
  N3: R3.Pin_0, Reed_Switch1.pin_1, Arduino1.D12/MISO
  N4: Reed_Switch1.pin_2, Arduino1.5V

notes:
  Reed switches close when a magnet is placed near their casing. In this example, a magnet could be mounted on a window and the reed switch on the windowsill so that everytime the window was opened, the piezo buzzer would sound.
  http://arduino.cc/en/Tutorial/Button
  http://arduino.cc/en/Tutorial/Melody
