# Fritzing sketch color-fader (saved by Fritzing 0.8.0b)
breadboards: 2

parts:
  R1 = Resistor [tolerance=±5% resistance=220 package=THT]
  R4 = Rotary Potentiometer (Small)
  Arduino1 = Arduino Uno (Rev3)
  LED1 = RGB LED (com. anode, rbg) [package="5 mm [THT]"]
  R3 = Resistor [tolerance=±5% resistance=220 package=THT]
  R2 = Resistor [tolerance=±5% resistance=220 package=THT]
  Arduino2 = Arduino Uno (Rev3)
  R5 = Resistor [tolerance=±5% resistance=220 package=THT]
  R6 = Resistor [tolerance=±5% resistance=220 package=THT]
  R7 = Resistor [tolerance=±5% resistance=220 package=THT]
  R8 = Rotary Potentiometer (Small)
  LED2 = RGB LED (com. cathode, rbg) [package="5 mm [THT]"]

nets:
  N1: R1.Pin_0, LED1.red_cathode
  N2: R1.Pin_1, Arduino1.D11_PWM/MOSI
  N3: R4.leg1, Arduino1.GND
  N4: R4.wiper, Arduino1.A0
  N5: R4.leg2, Arduino1.5V, LED1.common_anode
  N6: Arduino1.D9_PWM, R2.Pin_1
  N7: Arduino1.D10_PWM/SS, R3.Pin_1
  N8: LED1.blue_cathode, R3.Pin_0
  N9: LED1.green_cathode, R2.Pin_0
  N10: Arduino2.A0, R8.wiper
  N11: Arduino2.D9_PWM, R7.Pin_1
  N12: Arduino2.D10_PWM/SS, R6.Pin_1
  N13: Arduino2.D11_PWM/MOSI, R5.Pin_1
  N14: Arduino2.GND, R8.leg1, LED2.common_cathode
  N15: Arduino2.5V, R8.leg2
  N16: R5.Pin_0, LED2.red_anode
  N17: R6.Pin_0, LED2.blue_anode
  N18: R7.Pin_0, LED2.green_anode

notes:
  A potentiometer is used to display rainbow colors on an rgb LED.
  Get the Arduino-Code from here:
  http://fritzing.org/projects/color-fader/
  This is the same example, but using a "common cathode" RGB LED.
  Note that its long pin connects to - instead of +.
  This example is using the type in the Fritzing Starter Kits (pins: blue, common cathode, red, green).

// code stored in the sketch: color-fader.ino
/*
  _____       .__  __         .__                
_/ ____\______|__|/  |________|__| ____    ____  
\   __\\_  __ \  \   __\___   /  |/    \  / ___\ 
 |  |   |  | \/  ||  |  /    /|  |   |  \/ /_/  >
 |__|   |__|  |__||__| /_____ \__|___|  /\___  / 
                             \/       \//_____/  
          __                 __                  __   .__  __   
  _______/  |______ ________/  |_  ___________  |  | _|__|/  |_ 
 /  ___/\   __\__  \\_  __ \   __\/ __ \_  __ \ |  |/ /  \   __\
 \___ \  |  |  / __ \|  | \/|  | \  ___/|  | \/ |    <|  ||  |  
/____  > |__| (____  /__|   |__|  \___  >__|    |__|_ \__||__|  
     \/            \/                 \/             \/         

Example      RGB LED Fader
Autor        Stefan Hermann
Date         16.06.2011

Description  This example lets you fade through the colors of a RGB LED.

NOTE         This example expects an RGB LED of the type "common anode".
             If your type is "common cathode", the brightness will be reversed.

*/

int LEDGreen=9;
int LEDBlue=10;
int LEDRed=11;


int sensorPin=0;
int val;

void setup(){
  Serial.begin(9600);
  pinMode(LEDRed,OUTPUT);
  pinMode(LEDGreen,OUTPUT);
  pinMode(LEDBlue,OUTPUT);  
}

void loop(){
  
  val=map(analogRead(sensorPin),0,1024,0,900);
  Serial.println(val);
  if (val<150) {
    analogWrite(LEDRed,0);
    analogWrite(LEDBlue,255); 
    analogWrite(LEDGreen,255);    
  } else if (val<300) {
    analogWrite(LEDRed,map(val,150,300,0,255));
    analogWrite(LEDBlue,map(val,150,300,255,0)); 
    analogWrite(LEDGreen,255);
  } else if (val<450) {
    analogWrite(LEDRed,255);
    analogWrite(LEDBlue,0); 
    analogWrite(LEDGreen,255);  
  } else if (val<600) {
    analogWrite(LEDRed,255);
    analogWrite(LEDBlue,map(val,450,600,0,255)); 
    analogWrite(LEDGreen,map(val,450,600,255,0));
  } else if (val<750) {
    analogWrite(LEDRed,255);
    analogWrite(LEDBlue,255); 
    analogWrite(LEDGreen,0);  
  } else if (val<900) {
    analogWrite(LEDRed,map(val,750,900,255,0));
    analogWrite(LEDBlue,255); 
    analogWrite(LEDGreen,map(val,750,900,0,255));
  }
  delay(10);
}
