# Fritzing sketch Blink-SMD (saved by Fritzing 0.7.0b)

parts:
  LED1 = smd LED [color="Red (633nm)" package="0805 [SMD]"]
  Arduino2 = Arduino

nets:
  N1: LED1.cathode, Arduino2.GND
  N2: LED1.anode, Arduino2.D13

notes:
  In this very simple example, Arduino will be programmed to blink the LED on pin 13. Related example: http://arduino.cc/en/Tutorial/Blink

// code stored in the sketch: Blink-SMD.ino
/*
  Blink
  Turns on an LED on for one second, then off for one second, repeatedly.
 
  This example code is in the public domain.
 */

void setup() {                
  // initialize the digital pin as an output.
  // Pin 13 has an LED connected on most Arduino boards:
  pinMode(13, OUTPUT);     
}

void loop() {
  digitalWrite(13, HIGH);   // set the LED on
  delay(1000);              // wait for a second
  digitalWrite(13, LOW);    // set the LED off
  delay(1000);              // wait for a second
}
